// Logisim project Project5.circ as structural Verilog: 13 circuits, main circuit Computer
module Computer (
  input  [3:0] in_1,
  input  [3:0] in_2
);

  wire button_1_out, buzzercontroller_1_enablesound, clock_1_out, clock_2_out, clock_3_out, clock_4_out,
       cpu_1_buswriteenable, joystickcontroller_1_writetobus, keyboard_1_avail,
       keyboardcontroller_1_keyboardread, keyboardcontroller_1_writetobus, ledcontroller_1_datatoled,
       memorycontroller_1_writeenabletomem, memorycontroller_1_writetobus, rgb_video_1_p2,
       terminalcontroller_1_writetoterminal;
  wire [3:0] hexcontroller_1_datatoshow;
  wire [6:0] buzzercontroller_1_volume, keyboard_1_data, terminalcontroller_1_datatoterminal;
  wire [7:0] rgb_video_1_p3, rgb_video_1_p4;
  wire [13:0] buzzercontroller_1_frequency;
  wire [23:0] memorycontroller_1_addresstomem, rgb_video_1_p5;
  wire [25:0] cpu_1_addresstobus;
  wire [31:0] controlled_buffer_1_out, cpu_1_datatobus, joystickcontroller_1_datatobus,
       keyboardcontroller_1_datatobus, memorycontroller_1_datatobus, memorycontroller_1_datatomem, ram_1_dout;

  RAM #(.addrWidth(24), .dataWidth(32), .enables("line")) ram_1 (
    .addr(memorycontroller_1_addresstomem), .we(memorycontroller_1_writeenabletomem), .clk(clock_1_out),
    .din(memorycontroller_1_datatomem), .dout(ram_1_dout));
  Clock clock_1 (.out(clock_1_out));
  Joystick joystick_1 ();  // open: x, y
  // Probe on in_1
  // Probe on in_2
  Clock clock_2 (.out(clock_2_out));
  Keyboard keyboard_1 (
    .clk(clock_2_out), .re(keyboardcontroller_1_keyboardread), .avail(keyboard_1_avail),
    .data(keyboard_1_data));  // open: clr
  MemoryController memorycontroller_1 (
    .WriteEnableFromBus(cpu_1_buswriteenable), .DataFromBus(controlled_buffer_1_out),
    .AddressFromBus(cpu_1_addresstobus), .DataFromMem(ram_1_dout), .DataToMem(memorycontroller_1_datatomem),
    .WriteEnableToMem(memorycontroller_1_writeenabletomem), .WriteToBus(memorycontroller_1_writetobus),
    .AddressToMem(memorycontroller_1_addresstomem), .DataToBus(memorycontroller_1_datatobus));
  CPU cpu_1 (
    .DataFromBus(controlled_buffer_1_out), .AddressToBus(cpu_1_addresstobus),
    .BusWriteEnable(cpu_1_buswriteenable), .DataToBus(cpu_1_datatobus));
  assign controlled_buffer_1_out = memorycontroller_1_writetobus ? memorycontroller_1_datatobus : 32'bz;  // Controlled_Buffer controlled_buffer_1
  // Probe on memorycontroller_1_writetobus
  assign controlled_buffer_1_out = cpu_1_buswriteenable ? cpu_1_datatobus : 32'bz;  // Controlled_Buffer controlled_buffer_2
  // Probe on cpu_1_buswriteenable
  KeyboardController keyboardcontroller_1 (
    .KeyboardStatus(keyboard_1_avail), .WriteEnableFromBus(cpu_1_buswriteenable),
    .DataFromBus(controlled_buffer_1_out), .AddressFromBus(cpu_1_addresstobus),
    .KeyboardData(keyboard_1_data), .WriteToBus(keyboardcontroller_1_writetobus),
    .DataToBus(keyboardcontroller_1_datatobus), .KeyboardRead(keyboardcontroller_1_keyboardread));
  assign controlled_buffer_1_out = keyboardcontroller_1_writetobus ? keyboardcontroller_1_datatobus : 32'bz;  // Controlled_Buffer controlled_buffer_3
  // Probe on cpu_1_buswriteenable
  JoyStickController joystickcontroller_1 (
    .WEFromBus(cpu_1_buswriteenable), .AddressFromBus(cpu_1_addresstobus), .X(in_1), .Y(in_2),
    .WriteToBus(joystickcontroller_1_writetobus), .DataToBus(joystickcontroller_1_datatobus));  // open: DataFromBus
  assign controlled_buffer_1_out = joystickcontroller_1_writetobus ? joystickcontroller_1_datatobus : 32'bz;  // Controlled_Buffer controlled_buffer_4
  // Probe on joystickcontroller_1_writetobus
  // Probe on cpu_1_buswriteenable
  // Probe on cpu_1_addresstobus
  // Probe on controlled_buffer_1_out
  Clock clock_3 (.out(clock_3_out));
  // Probe on cpu_1_buswriteenable
  // Probe on cpu_1_buswriteenable
  // Probe on cpu_1_buswriteenable
  // Probe on cpu_1_buswriteenable
  // RGB_Video #(.height(256), .width(256)) rgb_video_1: pin names not known; wires that end beside it: clock_3_out, rgb_video_1_p2, rgb_video_1_p3, rgb_video_1_p4, rgb_video_1_p5
  TerminalController terminalcontroller_1 (
    .WriteEnableFromBus(cpu_1_buswriteenable), .AddressFromBus(cpu_1_addresstobus),
    .DataFromBus(controlled_buffer_1_out), .WriteToTerminal(terminalcontroller_1_writetoterminal),
    .DataToTerminal(terminalcontroller_1_datatoterminal));
  RGBController rgbcontroller_1 (
    .AddressFromBus(cpu_1_addresstobus), .DataFromBus(controlled_buffer_1_out),
    .WriteEnable(cpu_1_buswriteenable), .RGBX(rgb_video_1_p3), .RGBY(rgb_video_1_p4),
    .RGBColor(rgb_video_1_p5), .RGBWrite(rgb_video_1_p2));
  BuzzerController buzzercontroller_1 (
    .DataFromBus(controlled_buffer_1_out), .WE_FromBus(cpu_1_buswriteenable),
    .AddressFromBus(cpu_1_addresstobus), .Frequency(buzzercontroller_1_frequency),
    .EnableSound(buzzercontroller_1_enablesound), .Volume(buzzercontroller_1_volume));
  // Buzzer buzzer_1: pin names not known; wires that end beside it: buzzercontroller_1_frequency, buzzercontroller_1_enablesound, buzzercontroller_1_volume
  LED led_1 (.in(ledcontroller_1_datatoled));
  LEDController ledcontroller_1 (
    .DataFromBus(controlled_buffer_1_out), .AddressFromBus(cpu_1_addresstobus),
    .WriteEnableFromBus(cpu_1_buswriteenable), .DataToLED(ledcontroller_1_datatoled));
  HexController hexcontroller_1 (
    .DataFromBus(controlled_buffer_1_out), .AddressFromBus(cpu_1_addresstobus),
    .WriteEnable(cpu_1_buswriteenable), .DataToShow(hexcontroller_1_datatoshow));
  Hex_Digit_Display hex_digit_display_1 (.value(hexcontroller_1_datatoshow));  // open: dp
  TTY tty_1 (
    .data(terminalcontroller_1_datatoterminal), .clk(clock_4_out), .we(terminalcontroller_1_writetoterminal),
    .clr(button_1_out));
  Clock clock_4 (.out(clock_4_out));
  Button button_1 (.out(button_1_out));

  // Notes on the sheet:
  //   Write_enable
  //   Address
  //   Data
  //   Data
  //   WE
  //   Address
endmodule

module CPU (
  input  [31:0] DataFromBus,
  output [25:0] AddressToBus,
  output BusWriteEnable,
  output [31:0] DataToBus
);

  wire alu_1_equal, and_1_out, and_2_out, clock_1_out, comparator_1_eq, comparator_2_eq,
       control_1_alu_memsel, control_1_imm_sel, control_1_is_beq, control_1_is_bne, control_1_is_jr_jalr,
       control_1_is_jump, control_1_reg_we, not_1_out, or_1_out, or_2_out;
  wire [3:0] control_1_alu_code;
  wire [4:0] control_1_rd, control_1_rs, control_1_rt;
  wire [15:0] bit_extender_3_out, control_1_imm, multiplexer_8_out, shifter_1_out, shifter_4_out;
  wire [25:0] bit_extender_4_out, shifter_2_out;
  wire [31:0] adder_1_out, adder_2_out, bit_extender_1_out, bit_extender_2_out, bit_extender_5_out,
       multiplexer_1_out, multiplexer_2_out, multiplexer_3_out, multiplexer_4_out, multiplexer_5_out,
       multiplexer_6_out, multiplexer_7_out, ProgramCounter_q, regfile_1_rs_data, rom_1_data, shifter_3_out;
  wire [31:26] alu_1_res;

  Shifter #(.width(16)) shifter_1 (.in(control_1_imm), .\dist (4'b0010), .out(shifter_1_out));
  Shifter #(.width(26)) shifter_2 (.in(bit_extender_4_out), .\dist (5'b00010), .out(shifter_2_out));
  Adder #(.width(32)) adder_1 (.a(ProgramCounter_q), .b(32'h4), .out(adder_1_out));  // open: cin, cout
  assign bit_extender_1_out = {{16{shifter_1_out[15]}}, shifter_1_out};  // Bit_Extender bit_extender_1
  assign bit_extender_2_out = {{6{shifter_2_out[25]}}, shifter_2_out};  // Bit_Extender bit_extender_2
  Adder #(.width(32)) adder_2 (.a(adder_1_out), .b(bit_extender_1_out), .out(adder_2_out));  // open: cin, cout
  Multiplexer #(.width(32)) multiplexer_1 (
    .in0(bit_extender_2_out), .in1(regfile_1_rs_data), .out(multiplexer_1_out), .sel(control_1_is_jr_jalr));
  Multiplexer #(.width(32)) multiplexer_2 (
    .in0(adder_1_out), .in1(adder_2_out), .out(multiplexer_2_out), .sel(or_1_out));
  Multiplexer #(.width(32)) multiplexer_3 (
    .in0(multiplexer_2_out), .in1(multiplexer_1_out), .out(multiplexer_3_out), .sel(control_1_is_jump));
  Register #(.width(32)) ProgramCounter (
    .D(multiplexer_3_out), .clk(clock_1_out), .Q(ProgramCounter_q));  // open: en, clr
  Clock clock_1 (.out(clock_1_out));
  Bit_Extender #(.in_width(32)) bit_extender_3 (.in(shifter_3_out), .out(bit_extender_3_out));
  Shifter #(.shift("lr"), .width(32)) shifter_3 (.in(ProgramCounter_q), .\dist (5'b00010), .out(shifter_3_out));
  // Probe on ProgramCounter_q
  ROM #(.addrWidth(16), .dataWidth(32)) rom_1 (.addr(bit_extender_3_out), .data(rom_1_data));
  Bit_Extender #(.in_width(32), .out_width(26)) bit_extender_4 (.in(rom_1_data), .out(bit_extender_4_out));
  Multiplexer #(.width(32)) multiplexer_4 (
    .in0({alu_1_res, AddressToBus}), .in1(DataFromBus), .out(multiplexer_4_out), .sel(control_1_alu_memsel));
  // Probe on rom_1_data
  Multiplexer #(.width(32)) multiplexer_5 (
    .in0(multiplexer_4_out), .in1(adder_1_out), .out(multiplexer_5_out), .sel(control_1_is_jump));
  // Probe on rom_1_data[25:21]
  // Probe on rom_1_data[20:16]
  or or_1 (or_1_out, and_1_out, and_2_out);
  // Probe on rom_1_data[15:11]
  regfile regfile_1 (
    .rd(control_1_rd), .rt(control_1_rt), .rs(control_1_rs), .write_e(control_1_reg_we),
    .rd_data(multiplexer_5_out), .rs_data(regfile_1_rs_data), .rt_data(DataToBus));
  and and_1 (and_1_out, not_1_out, control_1_is_bne);
  and and_2 (and_2_out, alu_1_equal, control_1_is_beq);
  not not_1 (not_1_out, alu_1_equal);
  Control control_1 (
    .Instruction(rom_1_data), .rs(control_1_rs), .rt(control_1_rt), .rd(control_1_rd),
    .imm_sel(control_1_imm_sel), .imm(control_1_imm), .Reg_WE(control_1_reg_we),
    .ALU_code(control_1_alu_code), .ALU_MEMsel(control_1_alu_memsel), .we_mem(BusWriteEnable),
    .is_bne(control_1_is_bne), .is_beq(control_1_is_beq), .is_jump(control_1_is_jump),
    .is_jr_jalr(control_1_is_jr_jalr));
  Multiplexer #(.width(32)) multiplexer_6 (
    .in0(regfile_1_rs_data), .in1(DataToBus), .out(multiplexer_6_out), .sel(or_2_out));
  // Probe on DataToBus
  assign bit_extender_5_out = {{16{multiplexer_8_out[15]}}, multiplexer_8_out};  // Bit_Extender bit_extender_5
  // Probe on bit_extender_5_out
  // Probe on control_1_rs
  // Probe on control_1_rt
  // Probe on control_1_rd
  // Probe on control_1_imm_sel
  // Probe on control_1_imm
  Shifter #(.shift("lr"), .width(16)) shifter_4 (.in(control_1_imm), .\dist (4'b0110), .out(shifter_4_out));
  // Probe on multiplexer_6_out
  Multiplexer #(.width(32)) multiplexer_7 (
    .in0(DataToBus), .in1(bit_extender_5_out), .out(multiplexer_7_out), .sel(control_1_imm_sel));
  // Probe on multiplexer_7_out
  // Probe on control_1_alu_code
  Multiplexer #(.width(16)) multiplexer_8 (
    .in0(control_1_imm), .in1(shifter_4_out), .out(multiplexer_8_out), .sel(or_2_out));
  Comparator #(.width(4)) comparator_1 (.a(control_1_alu_code), .b(4'b0110), .eq(comparator_1_eq));  // open: gt, lt
  Comparator #(.width(4)) comparator_2 (.a(control_1_alu_code), .b(4'b0111), .eq(comparator_2_eq));  // open: gt, lt
  ALU alu_1 (
    .ALU_CODE(control_1_alu_code), .OP1(multiplexer_6_out), .OP2(multiplexer_7_out), .equal(alu_1_equal),
    .Res({alu_1_res, AddressToBus}));
  // Probe on {alu_1_res, AddressToBus}
  or or_2 (or_2_out, comparator_1_eq, comparator_2_eq);
  // Probe on DataToBus

  // Notes on the sheet:
  //   offset: word addressed
  //   PC + 4
  //   PC + 4 + Offset
  //   jr/jalr
  //   bne/beq
  //   any j*
  //   rs_data
  //   immediate
  //   contents of rom_1 (hex, n*v repeats v):
  //   1040001f 201b0001 105b0023 201b0010 105b004e 201b0011 105b004f 201b0004 105b0061 201b0005 105b006e
  //   201b0012 105b004c 201b0013 105b004d 201b0008 105b0096 201b0009 105b00b6 201b000a 105b00c2 201b000b
  //   105b00c1 201b000c 105b00c9 201b0014 105b0044 201b0015 105b0047 201b0016 105b0048 3400008 3c1d03ff
  //   37bdf000 201a0000 201b0004 af5b0000 80000ed 23bdffe8 afa80000 afa90004 afaa0008 afab000c afac0010
  //   afa40014 804020 100482a 11200005 200a002d 3c0b03ff 356bff00 ad6a0000 84022 11000011 2009000a 3a05020
  //   109001a 4012 5810 216b0030 214afffc ad4b0000 1500fff9 3c0b03ff 356bff00 8d4c0000 318c00ff ad6c0000
  //   214a0004 155dfffb 800004b 200c0030 3c0d03ff 35adff00 adac0000 8fa40014 8fac0010 8fab000c 8faa0008
  //   8fa90004 8fa80000 23bd0018 3400008 3084000f ac04ff30 3400008 8c02ff30 3042000f 3400008 8c02ff50
  //   3042000f 3400008 8c02ff54 3042000f 3400008 8c02ff50 8c03ff54 3042000f 3063000f 3400008 30840001
  //   ac04ff10 3400008 8c02ff10 30420001 3400008 23bdfff4 afa80000 afa90004 afa40008 804020 8d090000
  //   11200003 ac09ff00 21080004 800006f 8fa40008 8fa90004 8fa80000 23bd000c 3400008 23bdffe4 afa80000
  //   afa90004 afaa0008 afab000c afac0010 afad0014 afae0018 4020 4820 200a000a 8c0bff10 1160fffe 8c0dff14
  //   ac00ff10 200e000a 11ae0011 200e000d 11ae000f 200e002d 15ae0002 20090001 8000084 200e0030 1ae702a
  //   15c0fff1 200e003a 1ae702a 11c0ffee 21adffd0 10a0018 4012 10d4020 8000084 11200001 84022 1001020
  //   8fae0018 8fad0014 8fac0010 8fab000c 8faa0008 8fa90004 8fa80000 23bd001c 3400008 23bdffe4 afa80000
  //   afa90004 afaa0008 afab000c afac0010 afad0014 afa40018 200b0000 8d6c0000 1801020 8c09ff10 1120fffe
  //   8c0aff14 ac00ff10 2008000a 11480005 2008000d 11480003 ad8a0000 218c0004 80000b2 ad800000 218c0004
  //   ad6c0000 8fa40018 8fad0014 8fac0010 8fab000c 8faa0008 8fa90004 8fa80000 23bd001c 3400008 23bdfff4
  //   afa80000 afa90004 afa40008 20080000 8d090000 1201020 1244820 ad090000 8fa40008 8fa90004 8fa80000
  //   23bd000c 3400008 80000d7 23bdfff8 afa80000 afa40004 3c0803ff 3508ff00 ad040000 8fa40004 8fa80000
  //   23bd0008 3400008 23bdfff8 afa80000 afa90004 8c08ff10 1100fffe 8c02ff14 ac00ff10 8fa90004 8fa80000
  //   23bd0008 3400008 20130000 20140000 2002000b 20040043 d00c 2002000b 20040061 d00c 2002000b 2004006c
  //   d00c 2002000b 20040063 d00c 2002000b 2004003e d00c 2002000b 20040020 d00c 20020008 d00c 404020
  //   8d090000 312900ff 1120ffe8 200a0020 112a0007 200a0009 112a0005 200a0071 112a00df 200a0051 112a00dd
  //   8000112 21080004 8000104 8d090000 312900ff 200a005f 112a002a 200a002d 112a001c 200a002b 112a0020
  //   200a0030 12a582a 156000b9 200a003a 12a582a 116000b6 200d0000 200e0001 212cffd0 200f000a 1af0018 6812
  //   1ac6820 21080004 8d090000 312900ff 200a0030 12a582a 15600004 200a003a 12a582a 11600001 8000122
  //   1ae0018 8012 8000147 200effff 200d0000 21080004 8d090000 312900ff 8000122 200e0001 200d0000 21080004
  //   8d090000 312900ff 8000122 12800003 2608020 21080004 8000147 20100000 21080004 8000147 8d090000
  //   312900ff 1120ffa5 200a0020 112a0003 200a0009 112a0001 8000151 21080004 8000147 8d090000 312900ff
  //   1208820 21080004 8d090000 312900ff 1120ff97 200a0020 112a0003 200a0009 112a0001 800015f 21080004
  //   8000155 8d090000 312900ff 200a005f 112a002a 200a002d 112a001c 200a002b 112a0020 200a0030 12a582a
  //   1560006c 200a003a 12a582a 11600069 200d0000 200e0001 212cffd0 200f000a 1af0018 6812 1ac6820 21080004
  //   8d090000 312900ff 200a0030 12a582a 15600004 200a003a 12a582a 11600001 800016f 1ae0018 9012 8000194
  //   200effff 200d0000 21080004 8d090000 312900ff 800016f 200e0001 200d0000 21080004 8d090000 312900ff
  //   800016f 12800003 2609020 21080004 8000194 20120000 21080004 8000194 200a002b 122a0007 200a002d
  //   122a0009 200a002a 122a000b 200a002f 122a000e 80001d6 2124020 1009820 20140001 80001cf 2124022
  //   1009820 20140001 80001cf 2120018 4012 1009820 20140001 80001cf 12400005 212001a 4012 1009820
  //   20140001 80001cf 2002000b 20040045 d00c 2002000b 20040052 d00c 2002000b 20040052 d00c 2002000b
  //   2004003a d00c 2002000b 20040020 d00c 2002000b 20040064 d00c 2002000b 20040069 d00c 2002000b 20040076
  //   d00c 2002000b 20040030 d00c 2002000b 2004000a d00c 80000ef 1002020 20020001 d00c 2002000b 2004000a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
  //   label to jump to
  //   Tyeon Ford and Andy Quach
  //   BRANCH!
  //   ALU
  //   MEM
  //   PC + 4
  //   jal/jalr
  //   res value from ALU
  //   value from memory
  //   only write enable if the instruction should
  //   data from specified rs register
  //   data from specified rt register
  //   bne == 1 if the two registers are NOT equal
  //   beq == 1 if the two registers are equal
  //   rs register
  //   rt register
  //   rd register
  //   use imm?
  //   only if sll or srl
  //   move shamt
  //   from 10:6 to 3:0 
  //   only =1 if it is operating with an imm, otherwise operate with rt_data
  //   sll
  //   srl
  //   32 -> 26 bits
endmodule

module MemoryController (
  input  [31:0] DataFromBus,
  input  WriteEnableFromBus,
  input  [25:0] AddressFromBus,
  input  [31:0] DataFromMem,
  output [31:0] DataToMem,
  output WriteEnableToMem,
  output WriteToBus,
  output [23:0] AddressToMem,
  output [31:0] DataToBus
);

  wire comparator_1_lt, not_1_out;

  not not_1 (not_1_out, WriteEnableFromBus);
  Comparator #(.mode("unsigned"), .width(26)) comparator_1 (
    .a(AddressFromBus), .b(26'h3ffff00), .lt(comparator_1_lt));  // open: gt, eq
  assign DataToMem = WriteEnableToMem ? DataFromBus : 32'bz;  // Controlled_Buffer controlled_buffer_1
  and and_1 (WriteEnableToMem, WriteEnableFromBus, comparator_1_lt);
  and and_2 (WriteToBus, not_1_out, comparator_1_lt);

  assign AddressToMem = AddressFromBus[25:2];
  assign DataToBus = DataFromMem;

  // Notes on the sheet:
  //   Memory Controller
  //   Andy Quach & Tyeon Ford
  //   if RAM & WE=1 (sw)
  //   if RAM & WE=0 (lw)
  //   if addr < 0x3ffff00, RAM
  //   if in IO space, do nothing
endmodule

module KeyboardController (
  input  [31:0] DataFromBus,
  input  WriteEnableFromBus,
  input  [25:0] AddressFromBus,
  input  [6:0] KeyboardData,
  input  KeyboardStatus,
  output WriteToBus,
  output [31:0] DataToBus,
  output KeyboardRead
);

  wire and_1_out, and_2_out, and_3_out, clock_1_out, comparator_1_eq, comparator_2_eq,
       controlled_buffer_1_out, not_1_out, not_2_out, not_3_out;
  wire [6:0] bit_extender_3_out;
  wire [31:0] bit_extender_1_out, bit_extender_2_out, controlled_buffer_2_out;

  // Probe on KeyboardData
  Comparator #(.mode("unsigned"), .width(26)) comparator_1 (
    .a(26'h3ffff10), .b(AddressFromBus), .eq(comparator_1_eq));  // open: gt, lt
  Comparator #(.mode("unsigned"), .width(26)) comparator_2 (
    .a(AddressFromBus), .b(26'h3ffff14), .eq(comparator_2_eq));  // open: gt, lt
  TTY tty_1 (.data(KeyboardData), .clk(clock_1_out), .we(WriteToBus));  // open: clr
  Clock clock_1 (.out(clock_1_out));
  and and_1 (and_1_out, WriteEnableFromBus, comparator_1_eq);
  not not_1 (not_1_out, WriteEnableFromBus);
  and and_2 (and_2_out, not_1_out, comparator_2_eq);
  not not_2 (not_2_out, WriteEnableFromBus);
  and and_3 (and_3_out, not_2_out, comparator_1_eq);
  assign bit_extender_1_out = {{25{1'b0}}, KeyboardData};  // Bit_Extender bit_extender_1
  assign bit_extender_2_out = {{31{1'b0}}, KeyboardStatus};  // Bit_Extender bit_extender_2
  not not_3 (not_3_out, WriteEnableFromBus);
  Multiplexer #(.width(32)) multiplexer_1 (
    .in0(controlled_buffer_2_out), .in1(bit_extender_1_out), .out(DataToBus), .sel(controlled_buffer_1_out));
  assign controlled_buffer_1_out = not_3_out ? and_2_out : 1'bz;  // Controlled_Buffer controlled_buffer_1
  assign controlled_buffer_2_out = and_3_out ? bit_extender_2_out : 32'bz;  // Controlled_Buffer controlled_buffer_2
  Multiplexer multiplexer_2 (.in0(1'b0), .in1(WriteEnableFromBus), .out(KeyboardRead), .sel(and_1_out));
  or or_1 (WriteToBus, and_2_out, and_3_out);
  Bit_Extender #(.in_width(32), .out_width(7), .\type ("zero")) bit_extender_3 (
    .in(DataToBus), .out(bit_extender_3_out));
  TTY tty_2 (.data(bit_extender_3_out), .clk(clock_1_out), .we(WriteToBus));  // open: clr

  // Notes on the sheet:
  //   Keyboard Controller
  //   Andy Quach & Tyeon Ford
  //   if 0x3ffff10 & WE=0 (lw) -> keyb status to data bus
  //   if 0x3ffff10 & WE=1 (sw) -> send keyb read
  //   if 0x3ffff14 & WE=0 (lw) -> keyb data to data bus
  //   keyb read
  //   keyb data
  //   keyb status
endmodule

module RGBController (
  input  [25:0] AddressFromBus,
  input  [31:0] DataFromBus,
  input  WriteEnable,
  output [7:0] RGBX,
  output [7:0] RGBY,
  output [23:0] RGBColor,
  output RGBWrite
);

  wire and_1_out, and_2_out, and_3_out, clock_1_out, comparator_1_eq, comparator_2_eq, comparator_3_eq,
       comparator_4_eq;
  wire [7:0] bit_extender_1_out;
  wire [23:0] bit_extender_2_out;

  Comparator #(.mode("unsigned"), .width(26)) comparator_1 (
    .a(AddressFromBus), .b(26'h3ffff20), .eq(comparator_1_eq));  // open: gt, lt
  Comparator #(.mode("unsigned"), .width(26)) comparator_2 (
    .a(AddressFromBus), .b(26'h3ffff24), .eq(comparator_2_eq));  // open: gt, lt
  Comparator #(.mode("unsigned"), .width(26)) comparator_3 (
    .a(AddressFromBus), .b(26'h3ffff28), .eq(comparator_3_eq));  // open: gt, lt
  Comparator #(.mode("unsigned"), .width(26)) comparator_4 (
    .a(AddressFromBus), .b(26'h3ffff2c), .eq(comparator_4_eq));  // open: gt, lt
  Bit_Extender #(.in_width(32), .out_width(8)) bit_extender_1 (.in(DataFromBus), .out(bit_extender_1_out));
  Bit_Extender #(.in_width(32), .out_width(24)) bit_extender_2 (.in(DataFromBus), .out(bit_extender_2_out));
  Clock clock_1 (.out(clock_1_out));
  Register X (.D(bit_extender_1_out), .en(and_1_out), .clk(clock_1_out), .Q(RGBX));  // open: clr
  and and_1 (and_1_out, comparator_1_eq, WriteEnable);
  Register Y (.D(bit_extender_1_out), .en(and_2_out), .clk(clock_1_out), .Q(RGBY));  // open: clr
  and and_2 (and_2_out, comparator_2_eq, WriteEnable);
  and and_3 (and_3_out, comparator_3_eq, WriteEnable);
  Register #(.width(24)) RGB (.D(bit_extender_2_out), .en(and_3_out), .clk(clock_1_out), .Q(RGBColor));  // open: clr
  and and_4 (RGBWrite, comparator_4_eq, WriteEnable);

  // Notes on the sheet:
  //   RGB Controller
  //   Andy Quach & Tyeon Ford
  //   x cord
  //   y cord
  //   internal color
  //   WE
endmodule

module TerminalController (
  input  WriteEnableFromBus,
  input  [25:0] AddressFromBus,
  input  [31:0] DataFromBus,
  output WriteToTerminal,
  output [6:0] DataToTerminal
);

  wire button_1_out, clock_1_out, comparator_1_eq;
  wire [31:7] controlled_buffer_1_out;

  Comparator #(.mode("unsigned"), .width(26)) comparator_1 (
    .a(AddressFromBus), .b(26'h3ffff00), .eq(comparator_1_eq));  // open: gt, lt
  Clock clock_1 (.out(clock_1_out));
  and and_1 (WriteToTerminal, WriteEnableFromBus, comparator_1_eq);
  assign {controlled_buffer_1_out, DataToTerminal} = WriteToTerminal ? DataFromBus : 32'bz;  // Controlled_Buffer controlled_buffer_1
  TTY tty_1 (.data(DataToTerminal), .clk(clock_1_out), .we(WriteToTerminal), .clr(button_1_out));
  Button button_1 (.out(button_1_out));

  // Notes on the sheet:
  //   Terminal Controller
  //   Andy Quach & Tyeon Ford
  //   FOR TESTING
endmodule

module BuzzerController (
  input  [31:0] DataFromBus,
  input  WE_FromBus,
  input  [25:0] AddressFromBus,
  output [13:0] Frequency,
  output EnableSound,
  output [6:0] Volume
);

  wire and_1_out, and_2_out, and_3_out, clock_1_out, comparator_1_eq, comparator_2_eq, comparator_3_eq,
       not_1_out;
  wire [13:0] bit_extender_1_out, register_2_q;

  Bit_Extender #(.in_width(32), .out_width(14), .\type ("zero")) bit_extender_1 (
    .in(DataFromBus), .out(bit_extender_1_out));
  Comparator #(.mode("unsigned"), .width(26)) comparator_1 (
    .a(AddressFromBus), .b(26'h3ffff80), .eq(comparator_1_eq));  // open: gt, lt
  Comparator #(.mode("unsigned"), .width(26)) comparator_2 (
    .a(AddressFromBus), .b(26'h3ffff84), .eq(comparator_2_eq));  // open: gt, lt
  Comparator #(.mode("unsigned"), .width(26)) comparator_3 (
    .a(AddressFromBus), .b(26'h3ffff88), .eq(comparator_3_eq));  // open: gt, lt
  and and_1 (and_1_out, WE_FromBus, comparator_1_eq);
  and and_2 (and_2_out, WE_FromBus, comparator_2_eq);
  and and_3 (and_3_out, WE_FromBus, comparator_3_eq);
  Clock clock_1 (.out(clock_1_out));
  Register #(.width(14)) register_1 (
    .D(bit_extender_1_out), .en(and_1_out), .clk(clock_1_out), .Q(Frequency));  // open: clr
  Register #(.width(14)) register_2 (
    .D(bit_extender_1_out), .en(and_2_out), .clk(clock_1_out), .Q(register_2_q));  // open: clr
  Register #(.width(1)) register_3 (.D(not_1_out), .en(and_3_out), .clk(clock_1_out), .Q(EnableSound));  // open: clr
  not not_1 (not_1_out, EnableSound);
  Bit_Extender #(.in_width(14), .out_width(7), .\type ("zero")) bit_extender_2 (.in(register_2_q), .out(Volume));

  // Notes on the sheet:
  //   Buzzer Controller
  //   Andy Quach & Tyeon Ford
  //   3ffff80 + WE
  //   3ffff84 + WE
  //   3ffff88 + WE
  //   Current Setting
endmodule

module regfile (
  input  [31:0] rd_data,
  input  write_e,
  input  [4:0] rs,
  input  [4:0] rd,
  input  [4:0] rt,
  output [31:0] rs_data,
  output [31:0] rt_data
);

  wire and_1_out, and_2_out, and_3_out, and_4_out, and_5_out, and_6_out, and_7_out, and_8_out, and_9_out,
       and_10_out, and_11_out, and_12_out, and_13_out, and_14_out, and_15_out, and_16_out, and_17_out,
       and_18_out, and_19_out, and_20_out, and_21_out, and_22_out, and_23_out, and_24_out, and_25_out,
       and_26_out, and_27_out, and_28_out, and_29_out, and_30_out, and_31_out, clock_1_out,
       demultiplexer_1_out1, demultiplexer_1_out2, demultiplexer_1_out3, demultiplexer_1_out4,
       demultiplexer_1_out5, demultiplexer_1_out6, demultiplexer_1_out7, demultiplexer_1_out8,
       demultiplexer_1_out9, demultiplexer_1_out10, demultiplexer_1_out11, demultiplexer_1_out12,
       demultiplexer_1_out13, demultiplexer_1_out14, demultiplexer_1_out15, demultiplexer_1_out16,
       demultiplexer_1_out17, demultiplexer_1_out18, demultiplexer_1_out19, demultiplexer_1_out20,
       demultiplexer_1_out21, demultiplexer_1_out22, demultiplexer_1_out23, demultiplexer_1_out24,
       demultiplexer_1_out25, demultiplexer_1_out26, demultiplexer_1_out27, demultiplexer_1_out28,
       demultiplexer_1_out29, demultiplexer_1_out30, demultiplexer_1_out31;
  wire [31:0] register_1_q, register_2_q, register_3_q, register_4_q, register_5_q, register_6_q,
       register_7_q, register_8_q, register_9_q, register_10_q, register_11_q, register_12_q, register_13_q,
       register_14_q, register_15_q, register_16_q, register_17_q, register_18_q, register_19_q,
       register_20_q, register_21_q, register_22_q, register_23_q, register_24_q, register_25_q,
       register_26_q, register_27_q, register_28_q, register_29_q, register_30_q, register_31_q;

  Demultiplexer #(.select(5)) demultiplexer_1 (
    .out1(demultiplexer_1_out1), .out2(demultiplexer_1_out2), .out3(demultiplexer_1_out3),
    .out4(demultiplexer_1_out4), .out5(demultiplexer_1_out5), .out6(demultiplexer_1_out6),
    .out7(demultiplexer_1_out7), .out8(demultiplexer_1_out8), .out9(demultiplexer_1_out9),
    .out10(demultiplexer_1_out10), .out11(demultiplexer_1_out11), .out12(demultiplexer_1_out12),
    .out13(demultiplexer_1_out13), .out14(demultiplexer_1_out14), .out15(demultiplexer_1_out15),
    .out16(demultiplexer_1_out16), .out17(demultiplexer_1_out17), .out18(demultiplexer_1_out18),
    .out19(demultiplexer_1_out19), .out20(demultiplexer_1_out20), .out21(demultiplexer_1_out21),
    .out22(demultiplexer_1_out22), .out23(demultiplexer_1_out23), .out24(demultiplexer_1_out24),
    .out25(demultiplexer_1_out25), .out26(demultiplexer_1_out26), .out27(demultiplexer_1_out27),
    .out28(demultiplexer_1_out28), .out29(demultiplexer_1_out29), .out30(demultiplexer_1_out30),
    .out31(demultiplexer_1_out31), .in(1'b1), .sel(rd));  // open: out0
  Clock clock_1 (.out(clock_1_out));
  and and_1 (and_1_out, write_e, demultiplexer_1_out1);
  and and_2 (and_2_out, write_e, demultiplexer_1_out5);
  and and_3 (and_3_out, write_e, demultiplexer_1_out9);
  and and_4 (and_4_out, write_e, demultiplexer_1_out13);
  and and_5 (and_5_out, write_e, demultiplexer_1_out17);
  and and_6 (and_6_out, write_e, demultiplexer_1_out21);
  and and_7 (and_7_out, write_e, demultiplexer_1_out25);
  and and_8 (and_8_out, write_e, demultiplexer_1_out29);
  Register #(.width(32)) register_1 (.D(rd_data), .en(and_1_out), .clk(clock_1_out), .Q(register_1_q));  // open: clr
  Register #(.width(32)) register_2 (.D(rd_data), .en(and_2_out), .clk(clock_1_out), .Q(register_2_q));  // open: clr
  Register #(.width(32)) register_3 (.D(rd_data), .en(and_3_out), .clk(clock_1_out), .Q(register_3_q));  // open: clr
  Register #(.width(32)) register_4 (.D(rd_data), .en(and_4_out), .clk(clock_1_out), .Q(register_4_q));  // open: clr
  Register #(.width(32)) register_5 (.D(rd_data), .en(and_5_out), .clk(clock_1_out), .Q(register_5_q));  // open: clr
  Register #(.width(32)) register_6 (.D(rd_data), .en(and_6_out), .clk(clock_1_out), .Q(register_6_q));  // open: clr
  Register #(.width(32)) register_7 (.D(rd_data), .en(and_7_out), .clk(clock_1_out), .Q(register_7_q));  // open: clr
  Register #(.width(32)) register_8 (.D(rd_data), .en(and_8_out), .clk(clock_1_out), .Q(register_8_q));  // open: clr
  and and_9 (and_9_out, write_e, demultiplexer_1_out2);
  and and_10 (and_10_out, write_e, demultiplexer_1_out6);
  and and_11 (and_11_out, write_e, demultiplexer_1_out10);
  and and_12 (and_12_out, write_e, demultiplexer_1_out14);
  and and_13 (and_13_out, write_e, demultiplexer_1_out18);
  and and_14 (and_14_out, write_e, demultiplexer_1_out22);
  and and_15 (and_15_out, write_e, demultiplexer_1_out26);
  and and_16 (and_16_out, write_e, demultiplexer_1_out30);
  Register #(.width(32)) register_9 (.D(rd_data), .en(and_9_out), .clk(clock_1_out), .Q(register_9_q));  // open: clr
  Register #(.width(32)) register_10 (.D(rd_data), .en(and_10_out), .clk(clock_1_out), .Q(register_10_q));  // open: clr
  Register #(.width(32)) register_11 (.D(rd_data), .en(and_11_out), .clk(clock_1_out), .Q(register_11_q));  // open: clr
  Register #(.width(32)) register_12 (.D(rd_data), .en(and_12_out), .clk(clock_1_out), .Q(register_12_q));  // open: clr
  Register #(.width(32)) register_13 (.D(rd_data), .en(and_13_out), .clk(clock_1_out), .Q(register_13_q));  // open: clr
  Register #(.width(32)) register_14 (.D(rd_data), .en(and_14_out), .clk(clock_1_out), .Q(register_14_q));  // open: clr
  Register #(.width(32)) register_15 (.D(rd_data), .en(and_15_out), .clk(clock_1_out), .Q(register_15_q));  // open: clr
  Register #(.width(32)) register_16 (.D(rd_data), .en(and_16_out), .clk(clock_1_out), .Q(register_16_q));  // open: clr
  and and_17 (and_17_out, write_e, demultiplexer_1_out3);
  and and_18 (and_18_out, write_e, demultiplexer_1_out7);
  and and_19 (and_19_out, write_e, demultiplexer_1_out11);
  and and_20 (and_20_out, write_e, demultiplexer_1_out15);
  and and_21 (and_21_out, write_e, demultiplexer_1_out19);
  and and_22 (and_22_out, write_e, demultiplexer_1_out23);
  and and_23 (and_23_out, write_e, demultiplexer_1_out27);
  and and_24 (and_24_out, write_e, demultiplexer_1_out31);
  Register #(.width(32)) register_17 (.D(rd_data), .en(and_17_out), .clk(clock_1_out), .Q(register_17_q));  // open: clr
  Register #(.width(32)) register_18 (.D(rd_data), .en(and_18_out), .clk(clock_1_out), .Q(register_18_q));  // open: clr
  Register #(.width(32)) register_19 (.D(rd_data), .en(and_19_out), .clk(clock_1_out), .Q(register_19_q));  // open: clr
  Register #(.width(32)) register_20 (.D(rd_data), .en(and_20_out), .clk(clock_1_out), .Q(register_20_q));  // open: clr
  Register #(.width(32)) register_21 (.D(rd_data), .en(and_21_out), .clk(clock_1_out), .Q(register_21_q));  // open: clr
  Register #(.width(32)) register_22 (.D(rd_data), .en(and_22_out), .clk(clock_1_out), .Q(register_22_q));  // open: clr
  Register #(.width(32)) register_23 (.D(rd_data), .en(and_23_out), .clk(clock_1_out), .Q(register_23_q));  // open: clr
  Register #(.width(32)) register_24 (.D(rd_data), .en(and_24_out), .clk(clock_1_out), .Q(register_24_q));  // open: clr
  Register #(.width(32)) register_25 (.D(rd_data), .en(and_25_out), .clk(clock_1_out), .Q(register_25_q));  // open: clr
  and and_25 (and_25_out, write_e, demultiplexer_1_out4);
  Register #(.width(32)) register_26 (.D(rd_data), .en(and_26_out), .clk(clock_1_out), .Q(register_26_q));  // open: clr
  and and_26 (and_26_out, write_e, demultiplexer_1_out8);
  Register #(.width(32)) register_27 (.D(rd_data), .en(and_27_out), .clk(clock_1_out), .Q(register_27_q));  // open: clr
  and and_27 (and_27_out, write_e, demultiplexer_1_out12);
  Register #(.width(32)) register_28 (.D(rd_data), .en(and_28_out), .clk(clock_1_out), .Q(register_28_q));  // open: clr
  and and_28 (and_28_out, write_e, demultiplexer_1_out16);
  Register #(.width(32)) register_29 (.D(rd_data), .en(and_29_out), .clk(clock_1_out), .Q(register_29_q));  // open: clr
  and and_29 (and_29_out, write_e, demultiplexer_1_out20);
  Register #(.width(32)) register_30 (.D(rd_data), .en(and_30_out), .clk(clock_1_out), .Q(register_30_q));  // open: clr
  and and_30 (and_30_out, write_e, demultiplexer_1_out24);
  Register #(.width(32)) register_31 (.D(rd_data), .en(and_31_out), .clk(clock_1_out), .Q(register_31_q));  // open: clr
  and and_31 (and_31_out, write_e, demultiplexer_1_out28);
  Multiplexer #(.select(5), .width(32)) multiplexer_1 (
    .in0({32{1'b0}}), .in1(register_1_q), .in2(register_9_q), .in3(register_17_q), .in4(register_25_q),
    .in5(register_2_q), .in6(register_10_q), .in7(register_18_q), .in8(register_26_q), .in9(register_3_q),
    .in10(register_11_q), .in11(register_19_q), .in12(register_27_q), .in13(register_4_q),
    .in14(register_12_q), .in15(register_20_q), .in16(register_28_q), .in17(register_5_q),
    .in18(register_13_q), .in19(register_21_q), .in20(register_29_q), .in21(register_6_q),
    .in22(register_14_q), .in23(register_22_q), .in24(register_30_q), .in25(register_7_q),
    .in26(register_15_q), .in27(register_23_q), .in28(register_31_q), .in29(register_8_q),
    .in30(register_16_q), .in31(register_24_q), .out(rs_data), .sel(rs));
  Multiplexer #(.select(5), .width(32)) multiplexer_2 (
    .in0({32{1'b0}}), .in1(register_1_q), .in2(register_9_q), .in3(register_17_q), .in4(register_25_q),
    .in5(register_2_q), .in6(register_10_q), .in7(register_18_q), .in8(register_26_q), .in9(register_3_q),
    .in10(register_11_q), .in11(register_19_q), .in12(register_27_q), .in13(register_4_q),
    .in14(register_12_q), .in15(register_20_q), .in16(register_28_q), .in17(register_5_q),
    .in18(register_13_q), .in19(register_21_q), .in20(register_29_q), .in21(register_6_q),
    .in22(register_14_q), .in23(register_22_q), .in24(register_30_q), .in25(register_7_q),
    .in26(register_15_q), .in27(register_23_q), .in28(register_31_q), .in29(register_8_q),
    .in30(register_16_q), .in31(register_24_q), .out(rt_data), .sel(rt));

  // Notes on the sheet:
  //   Tyeon Ford and Andy Quach
  //   (can't write to zero register since it should be constant)
  //   To decide which register to write data to
  //   Will only write to a register if the instruction should at all
  //   and if that register is specifically chosen
  //   The data that will be written to a register
  //   $at
  //   $a1
  //   $t1
  //   $t5
  //   $s1
  //   $s5
  //   $t9
  //   $sp
  //   $v0
  //   $a2
  //   $t2
  //   $t6
  //   $s2
  //   $s6
  //   $k0
  //   $v1
  //   $a3
  //   $t3
  //   $t7
  //   $s3
  //   $s7
  //   $ra
  //   $a0
  //   $t0
  //   $t4
  //   $s0
  //   $s4
  //   $t8
  //   zero register should always output 0
  //   Reads the data from a specific source register
  //   Reads the data from a specific register
endmodule

module ALU (
  input  [3:0] ALU_CODE,
  input  [31:0] OP1,
  input  [31:0] OP2,
  output [31:0] Res,
  output equal
);

  wire clock_1_out, comparator_1_lt, comparator_3_eq, comparator_4_eq, or_2_out;
  wire [4:0] bit_extender_1_out, bit_extender_2_out;
  wire [31:0] adder_1_out, and_1_out, bit_extender_3_out, divider_1_out, divider_1_rem, HI_q, LO_q,
       multiplexer_1_out, multiplexer_2_out, multiplier_1_cout, multiplier_1_out, nor_1_out, or_1_out,
       shifter_1_out, shifter_2_out, shifter_3_out, subtractor_1_out, xor_1_out;

  Clock clock_1 (.out(clock_1_out));
  Bit_Extender #(.in_width(32), .out_width(5), .\type ("zero")) bit_extender_1 (.in(OP2), .out(bit_extender_1_out));
  Bit_Extender #(.in_width(32), .out_width(5), .\type ("zero")) bit_extender_2 (.in(OP2), .out(bit_extender_2_out));
  Adder #(.width(32)) adder_1 (.a(OP1), .b(OP2), .out(adder_1_out));  // open: cin, cout
  Subtractor #(.width(32)) subtractor_1 (.a(OP1), .b(OP2), .out(subtractor_1_out));  // open: bin, bout
  Shifter #(.width(32)) shifter_1 (.in(OP1), .\dist (bit_extender_1_out), .out(shifter_1_out));
  Shifter #(.shift("lr"), .width(32)) shifter_2 (.in(OP1), .\dist (bit_extender_2_out), .out(shifter_2_out));
  Comparator #(.width(32)) comparator_1 (.a(OP1), .b(OP2), .lt(comparator_1_lt));  // open: gt, eq
  assign and_1_out = OP1 & OP2;  // AND_Gate and_1, 32 bits wide
  assign or_1_out = OP1 | OP2;  // OR_Gate or_1, 32 bits wide
  assign nor_1_out = ~(OP1 | OP2);  // NOR_Gate nor_1, 32 bits wide
  assign xor_1_out = OP1 ^ OP2;  // XOR_Gate xor_1, 32 bits wide
  Shifter #(.width(32)) shifter_3 (.in(OP1), .\dist (5'b10000), .out(shifter_3_out));
  Comparator #(.width(32)) comparator_2 (.a(OP1), .b(OP2), .eq(equal));  // open: gt, lt
  Multiplier #(.width(32)) multiplier_1 (
    .a(OP1), .b(OP2), .out(multiplier_1_out), .cout(multiplier_1_cout));  // open: cin
  Divider #(.mode("twosComplement"), .width(32)) divider_1 (
    .a(OP1), .b(OP2), .out(divider_1_out), .rem(divider_1_rem));  // open: upper
  assign bit_extender_3_out = {{31{1'b0}}, comparator_1_lt};  // Bit_Extender bit_extender_3
  Multiplexer #(.width(32)) multiplexer_1 (
    .in0(multiplier_1_out), .in1(divider_1_out), .out(multiplexer_1_out), .sel(comparator_4_eq));
  Multiplexer #(.width(32)) multiplexer_2 (
    .in0(multiplier_1_cout), .in1(divider_1_rem), .out(multiplexer_2_out), .sel(comparator_4_eq));
  Comparator #(.width(4)) comparator_3 (.a(ALU_CODE), .b(4'b0010), .eq(comparator_3_eq));  // open: gt, lt
  Comparator #(.width(4)) comparator_4 (.a(ALU_CODE), .b(4'b0011), .eq(comparator_4_eq));  // open: gt, lt
  or or_2 (or_2_out, comparator_3_eq, comparator_4_eq);
  Register #(.width(32)) LO (.D(multiplexer_1_out), .en(or_2_out), .clk(clock_1_out), .Q(LO_q));  // open: clr
  Register #(.width(32)) HI (.D(multiplexer_2_out), .en(or_2_out), .clk(clock_1_out), .Q(HI_q));  // open: clr
  Multiplexer #(.select(4), .width(32)) multiplexer_3 (
    .in0(adder_1_out), .in1(subtractor_1_out), .in4(LO_q), .in5(HI_q), .in6(shifter_1_out),
    .in7(shifter_2_out), .in8(bit_extender_3_out), .in9(and_1_out), .in10(or_1_out), .in11(nor_1_out),
    .in12(xor_1_out), .in13(shifter_3_out), .out(Res), .sel(ALU_CODE));  // open: in2, in3, in14, in15

  // Notes on the sheet:
  //   Andy Quach and Tyeon Ford
  //   add/addi
  //   subtract
  //   sll
  //   srl
  //   AND
  //   OR
  //   LUI
  //   slt
  //   NOR
  //   XOR
  //   Product
  //   Overflow
  //   Quotient
  //   Remainder
endmodule

module Control (
  input  [31:0] Instruction,
  output [4:0] rs,
  output [4:0] rt,
  output [4:0] rd,
  output imm_sel,
  output [15:0] imm,
  output Reg_WE,
  output [3:0] ALU_code,
  output ALU_MEMsel,
  output we_mem,
  output is_bne,
  output is_beq,
  output is_jump,
  output is_jr_jalr
);

  wire and_1_out, and_2_out, and_3_out, comparator_1_eq, comparator_2_eq, comparator_3_eq, comparator_4_eq,
       comparator_5_eq, comparator_6_eq, comparator_7_eq, comparator_8_eq, comparator_9_eq, comparator_10_eq,
       comparator_11_eq, comparator_12_eq, comparator_13_eq, comparator_14_eq, comparator_15_eq,
       comparator_16_eq, comparator_17_eq, comparator_18_eq, comparator_19_eq, comparator_24_eq,
       comparator_25_eq, comparator_26_eq, comparator_27_eq, comparator_28_eq, comparator_29_eq,
       comparator_30_eq, comparator_31_eq, not_1_out, not_2_out, not_3_out, not_4_out, or_2_out, or_3_out,
       or_4_out, or_5_out, or_6_out, or_9_out, or_11_out, or_12_out;
  wire [3:0] adder_1_out, adder_2_out, adder_3_out, adder_4_out, adder_5_out, adder_6_out, adder_7_out,
       adder_8_out, adder_9_out, adder_10_out, adder_11_out, adder_12_out, adder_13_out, adder_14_out,
       demultiplexer_4_out0, demultiplexer_4_out1, demultiplexer_5_out0, demultiplexer_5_out1,
       demultiplexer_6_out0, demultiplexer_6_out1, demultiplexer_7_out0, demultiplexer_7_out1,
       demultiplexer_8_out0, demultiplexer_8_out1, demultiplexer_9_out0, demultiplexer_9_out1,
       demultiplexer_10_out0, demultiplexer_10_out1, demultiplexer_11_out0, demultiplexer_11_out1,
       demultiplexer_12_out0, demultiplexer_12_out1, demultiplexer_13_out0, demultiplexer_13_out1,
       demultiplexer_14_out0, demultiplexer_14_out1, demultiplexer_15_out0, demultiplexer_15_out1,
       demultiplexer_16_out0, demultiplexer_16_out1, demultiplexer_17_out0, demultiplexer_17_out1,
       multiplexer_2_out, multiplexer_3_out, multiplexer_4_out, multiplexer_5_out, multiplexer_6_out,
       multiplexer_7_out, multiplexer_8_out, multiplexer_9_out, multiplexer_10_out, multiplexer_11_out,
       multiplexer_12_out, multiplexer_13_out, multiplexer_14_out, multiplexer_15_out, or_10_out;
  wire [4:0] demultiplexer_1_out1, demultiplexer_2_out0, demultiplexer_2_out1, multiplexer_1_out,
       multiplexer_16_out, multiplexer_17_out;
  wire [5:0] demultiplexer_3_out1;

  // Probe on Instruction[5:0]
  // Probe on Instruction[10:6]
  // Probe on Instruction[15:11]
  // Probe on Instruction[20:16]
  // Probe on Instruction[25:21]
  Comparator #(.width(6)) comparator_1 (.a({6{1'b0}}), .b(Instruction[31:26]), .eq(comparator_1_eq));  // open: gt, lt
  Comparator #(.width(1)) comparator_2 (.a(1'b0), .b(comparator_1_eq), .eq(comparator_2_eq));  // open: gt, lt
  Demultiplexer #(.width(5)) demultiplexer_1 (
    .out0(imm[15:11]), .out1(demultiplexer_1_out1), .in(Instruction[15:11]), .sel(comparator_1_eq));
  Demultiplexer #(.width(5)) demultiplexer_2 (
    .out0(demultiplexer_2_out0), .out1(demultiplexer_2_out1), .in(Instruction[10:6]), .sel(comparator_1_eq));
  Demultiplexer #(.width(6)) demultiplexer_3 (
    .out0(imm[5:0]), .out1(demultiplexer_3_out1), .in(Instruction[5:0]), .sel(comparator_1_eq));
  assign imm[10:6] = demultiplexer_2_out0 | demultiplexer_2_out1;  // OR_Gate or_1, 5 bits wide
  not not_1 (not_1_out, comparator_2_eq);
  Comparator #(.width(6)) comparator_3 (.a(6'b100000), .b(demultiplexer_3_out1), .eq(comparator_3_eq));  // open: gt, lt
  Comparator #(.width(6)) comparator_4 (.a(6'b100010), .b(demultiplexer_3_out1), .eq(comparator_4_eq));  // open: gt, lt
  Comparator #(.width(6)) comparator_5 (.a(6'b011000), .b(demultiplexer_3_out1), .eq(comparator_5_eq));  // open: gt, lt
  Comparator #(.width(6)) comparator_6 (.a(6'b011010), .b(demultiplexer_3_out1), .eq(comparator_6_eq));  // open: gt, lt
  Comparator #(.width(6)) comparator_7 (.a(6'b010010), .b(demultiplexer_3_out1), .eq(comparator_7_eq));  // open: gt, lt
  Comparator #(.width(6)) comparator_8 (.a(6'b010000), .b(demultiplexer_3_out1), .eq(comparator_8_eq));  // open: gt, lt
  Comparator #(.width(6)) comparator_9 (.a({6{1'b0}}), .b(demultiplexer_3_out1), .eq(comparator_9_eq));  // open: gt, lt
  and and_1 (and_1_out, comparator_9_eq, not_1_out);
  Comparator #(.width(6)) comparator_10 (
    .a(6'b000010), .b(demultiplexer_3_out1), .eq(comparator_10_eq));  // open: gt, lt
  Comparator #(.width(6)) comparator_11 (
    .a(6'b101010), .b(demultiplexer_3_out1), .eq(comparator_11_eq));  // open: gt, lt
  Comparator #(.width(6)) comparator_12 (
    .a(6'b100100), .b(demultiplexer_3_out1), .eq(comparator_12_eq));  // open: gt, lt
  or or_2 (or_2_out, comparator_12_eq, comparator_13_eq);
  Comparator #(.width(6)) comparator_13 (.a(6'b001100), .b(Instruction[31:26]), .eq(comparator_13_eq));  // open: gt, lt
  Comparator #(.width(6)) comparator_14 (
    .a(6'b100101), .b(demultiplexer_3_out1), .eq(comparator_14_eq));  // open: gt, lt
  Comparator #(.width(6)) comparator_15 (.a(6'b001101), .b(Instruction[31:26]), .eq(comparator_15_eq));  // open: gt, lt
  Comparator #(.width(6)) comparator_16 (
    .a(6'b100110), .b(demultiplexer_3_out1), .eq(comparator_16_eq));  // open: gt, lt
  Comparator #(.width(6)) comparator_17 (.a(6'b001110), .b(Instruction[31:26]), .eq(comparator_17_eq));  // open: gt, lt
  Comparator #(.width(6)) comparator_18 (
    .a(6'b100111), .b(demultiplexer_3_out1), .eq(comparator_18_eq));  // open: gt, lt
  Comparator #(.width(6)) comparator_19 (.a(6'b001111), .b(Instruction[31:26]), .eq(comparator_19_eq));  // open: gt, lt
  Comparator #(.width(6)) comparator_20 (.a(6'b100011), .b(Instruction[31:26]), .eq(ALU_MEMsel));  // open: gt, lt
  Comparator #(.width(6)) comparator_21 (.a(6'b101011), .b(Instruction[31:26]), .eq(we_mem));  // open: gt, lt
  Comparator #(.width(6)) comparator_22 (.a(6'b000101), .b(Instruction[31:26]), .eq(is_bne));  // open: gt, lt
  Comparator #(.width(6)) comparator_23 (.a(6'b000100), .b(Instruction[31:26]), .eq(is_beq));  // open: gt, lt
  Comparator #(.width(6)) comparator_24 (.a(6'b000010), .b(Instruction[31:26]), .eq(comparator_24_eq));  // open: gt, lt
  Comparator #(.width(6)) comparator_25 (.a(6'b000011), .b(Instruction[31:26]), .eq(comparator_25_eq));  // open: gt, lt
  Comparator #(.width(6)) comparator_26 (
    .a(6'b001000), .b(demultiplexer_3_out1), .eq(comparator_26_eq));  // open: gt, lt
  Comparator #(.width(6)) comparator_27 (
    .a(6'b001001), .b(demultiplexer_3_out1), .eq(comparator_27_eq));  // open: gt, lt
  Comparator #(.width(6)) comparator_28 (
    .a(6'b001100), .b(demultiplexer_3_out1), .eq(comparator_28_eq));  // open: gt, lt
  Demultiplexer #(.width(4)) demultiplexer_4 (
    .out0(demultiplexer_4_out0), .out1(demultiplexer_4_out1), .in(4'b0000), .sel(comparator_3_eq));
  Demultiplexer #(.width(4)) demultiplexer_5 (
    .out0(demultiplexer_5_out0), .out1(demultiplexer_5_out1), .in(adder_1_out), .sel(comparator_4_eq));
  Demultiplexer #(.width(4)) demultiplexer_6 (
    .out0(demultiplexer_6_out0), .out1(demultiplexer_6_out1), .in(adder_2_out), .sel(comparator_5_eq));
  Demultiplexer #(.width(4)) demultiplexer_7 (
    .out0(demultiplexer_7_out0), .out1(demultiplexer_7_out1), .in(adder_3_out), .sel(comparator_6_eq));
  Demultiplexer #(.width(4)) demultiplexer_8 (
    .out0(demultiplexer_8_out0), .out1(demultiplexer_8_out1), .in(adder_4_out), .sel(comparator_7_eq));
  Demultiplexer #(.width(4)) demultiplexer_9 (
    .out0(demultiplexer_9_out0), .out1(demultiplexer_9_out1), .in(adder_5_out), .sel(comparator_8_eq));
  Demultiplexer #(.width(4)) demultiplexer_10 (
    .out0(demultiplexer_10_out0), .out1(demultiplexer_10_out1), .in(adder_6_out), .sel(and_1_out));
  Demultiplexer #(.width(4)) demultiplexer_11 (
    .out0(demultiplexer_11_out0), .out1(demultiplexer_11_out1), .in(adder_7_out), .sel(comparator_10_eq));
  Demultiplexer #(.width(4)) demultiplexer_12 (
    .out0(demultiplexer_12_out0), .out1(demultiplexer_12_out1), .in(adder_8_out), .sel(comparator_11_eq));
  Demultiplexer #(.width(4)) demultiplexer_13 (
    .out0(demultiplexer_13_out0), .out1(demultiplexer_13_out1), .in(adder_9_out), .sel(or_2_out));
  Demultiplexer #(.width(4)) demultiplexer_14 (
    .out0(demultiplexer_14_out0), .out1(demultiplexer_14_out1), .in(adder_10_out), .sel(or_3_out));
  or or_3 (or_3_out, comparator_14_eq, comparator_15_eq);
  Demultiplexer #(.width(4)) demultiplexer_15 (
    .out0(demultiplexer_15_out0), .out1(demultiplexer_15_out1), .in(adder_11_out), .sel(or_4_out));
  or or_4 (or_4_out, comparator_16_eq, comparator_17_eq);
  Demultiplexer #(.width(4)) demultiplexer_16 (
    .out0(demultiplexer_16_out0), .out1(demultiplexer_16_out1), .in(adder_12_out), .sel(comparator_18_eq));
  Demultiplexer #(.width(4)) demultiplexer_17 (
    .out0(demultiplexer_17_out0), .out1(demultiplexer_17_out1), .in(adder_13_out), .sel(comparator_19_eq));
  or or_5 (or_5_out, comparator_27_eq, comparator_28_eq);
  Comparator #(.width(6)) comparator_29 (.a(Instruction[31:26]), .b(6'b000100), .eq(comparator_29_eq));  // open: gt, lt
  Comparator #(.width(6)) comparator_30 (.a(Instruction[31:26]), .b(6'b000101), .eq(comparator_30_eq));  // open: gt, lt
  or or_6 (or_6_out, comparator_29_eq, comparator_30_eq);
  Adder #(.width(4)) adder_1 (.a(demultiplexer_4_out0), .b(4'b0001), .out(adder_1_out));  // open: cin, cout
  Adder #(.width(4)) adder_2 (.a(demultiplexer_5_out0), .b(4'b0001), .out(adder_2_out));  // open: cin, cout
  Adder #(.width(4)) adder_3 (.a(demultiplexer_6_out0), .b(4'b0001), .out(adder_3_out));  // open: cin, cout
  Adder #(.width(4)) adder_4 (.a(demultiplexer_7_out0), .b(4'b0001), .out(adder_4_out));  // open: cin, cout
  Adder #(.width(4)) adder_5 (.a(demultiplexer_8_out0), .b(4'b0001), .out(adder_5_out));  // open: cin, cout
  Adder #(.width(4)) adder_6 (.a(demultiplexer_9_out0), .b(4'b0001), .out(adder_6_out));  // open: cin, cout
  Adder #(.width(4)) adder_7 (.a(demultiplexer_10_out0), .b(4'b0001), .out(adder_7_out));  // open: cin, cout
  Adder #(.width(4)) adder_8 (.a(demultiplexer_11_out0), .b(4'b0001), .out(adder_8_out));  // open: cin, cout
  Adder #(.width(4)) adder_9 (.a(demultiplexer_12_out0), .b(4'b0001), .out(adder_9_out));  // open: cin, cout
  Adder #(.width(4)) adder_10 (.a(demultiplexer_13_out0), .b(4'b0001), .out(adder_10_out));  // open: cin, cout
  Adder #(.width(4)) adder_11 (.a(demultiplexer_14_out0), .b(4'b0001), .out(adder_11_out));  // open: cin, cout
  Adder #(.width(4)) adder_12 (.a(demultiplexer_15_out0), .b(4'b0001), .out(adder_12_out));  // open: cin, cout
  Adder #(.width(4)) adder_13 (.a(demultiplexer_16_out0), .b(4'b0001), .out(adder_13_out));  // open: cin, cout
  Adder #(.width(4)) adder_14 (.a(demultiplexer_17_out0), .b(4'b0001), .out(adder_14_out));  // open: cin, cout
  Multiplexer #(.width(5)) multiplexer_1 (
    .in0(Instruction[20:16]), .in1(demultiplexer_1_out1), .out(multiplexer_1_out), .sel(comparator_1_eq));
  not not_2 (not_2_out, or_6_out);
  not not_3 (not_3_out, comparator_1_eq);
  and and_2 (and_2_out, not_2_out, not_3_out);
  Comparator #(.width(5)) comparator_31 (
    .a({5{1'b0}}), .b(demultiplexer_1_out1), .eq(comparator_31_eq));  // open: gt, lt
  Multiplexer #(.width(4)) multiplexer_2 (
    .in0(4'b0000), .in1(demultiplexer_4_out1), .out(multiplexer_2_out), .sel(comparator_3_eq));
  Multiplexer #(.width(4)) multiplexer_3 (
    .in0(4'b0000), .in1(demultiplexer_5_out1), .out(multiplexer_3_out), .sel(comparator_4_eq));
  Multiplexer #(.width(4)) multiplexer_4 (
    .in0(4'b0000), .in1(demultiplexer_6_out1), .out(multiplexer_4_out), .sel(comparator_5_eq));
  Multiplexer #(.width(4)) multiplexer_5 (
    .in0(4'b0000), .in1(demultiplexer_7_out1), .out(multiplexer_5_out), .sel(comparator_6_eq));
  Multiplexer #(.width(4)) multiplexer_6 (
    .in0(4'b0000), .in1(demultiplexer_8_out1), .out(multiplexer_6_out), .sel(comparator_7_eq));
  Multiplexer #(.width(4)) multiplexer_7 (
    .in0(4'b0000), .in1(demultiplexer_9_out1), .out(multiplexer_7_out), .sel(comparator_8_eq));
  Multiplexer #(.width(4)) multiplexer_8 (
    .in0(4'b0000), .in1(demultiplexer_10_out1), .out(multiplexer_8_out), .sel(and_1_out));
  Multiplexer #(.width(4)) multiplexer_9 (
    .in0(4'b0000), .in1(demultiplexer_11_out1), .out(multiplexer_9_out), .sel(comparator_10_eq));
  Multiplexer #(.width(4)) multiplexer_10 (
    .in0(4'b0000), .in1(demultiplexer_12_out1), .out(multiplexer_10_out), .sel(comparator_11_eq));
  Multiplexer #(.width(4)) multiplexer_11 (
    .in0(4'b0000), .in1(demultiplexer_13_out1), .out(multiplexer_11_out), .sel(or_2_out));
  Multiplexer #(.width(4)) multiplexer_12 (
    .in0(4'b0000), .in1(demultiplexer_14_out1), .out(multiplexer_12_out), .sel(or_3_out));
  Multiplexer #(.width(4)) multiplexer_13 (
    .in0(4'b0000), .in1(demultiplexer_15_out1), .out(multiplexer_13_out), .sel(or_4_out));
  Multiplexer #(.width(4)) multiplexer_14 (
    .in0(4'b0000), .in1(demultiplexer_16_out1), .out(multiplexer_14_out), .sel(comparator_18_eq));
  Multiplexer #(.width(4)) multiplexer_15 (
    .in0(4'b0000), .in1(demultiplexer_17_out1), .out(multiplexer_15_out), .sel(comparator_19_eq));
  or or_7 (imm_sel, and_2_out, or_9_out);
  or or_8 (is_jr_jalr, comparator_26_eq, or_5_out);
  or or_9 (or_9_out, and_1_out, comparator_10_eq);
  assign or_10_out = multiplexer_14_out | multiplexer_6_out | multiplexer_13_out | multiplexer_11_out | multiplexer_2_out | multiplexer_3_out | multiplexer_4_out | multiplexer_5_out | multiplexer_15_out | multiplexer_7_out | multiplexer_8_out | multiplexer_9_out | multiplexer_10_out | multiplexer_12_out;  // OR_Gate or_10, 4 bits wide
  not not_4 (not_4_out, comparator_1_eq);
  or or_11 (or_11_out, comparator_13_eq, comparator_15_eq, comparator_17_eq, comparator_19_eq);
  Multiplexer #(.width(5)) multiplexer_16 (
    .in0(multiplexer_1_out), .in1({5{1'b1}}), .out(multiplexer_16_out), .sel(comparator_25_eq));
  Multiplexer #(.width(5)) multiplexer_17 (
    .in0(demultiplexer_1_out1), .in1({5{1'b1}}), .out(multiplexer_17_out), .sel(comparator_31_eq));
  and and_3 (and_3_out, not_4_out, or_11_out);
  Multiplexer #(.width(5)) multiplexer_18 (
    .in0(multiplexer_16_out), .in1(multiplexer_17_out), .out(rd), .sel(or_5_out));
  Multiplexer #(.width(4)) multiplexer_19 (.in0(4'b0000), .in1(or_10_out), .out(ALU_code), .sel(or_12_out));
  or or_12 (or_12_out, comparator_1_eq, and_3_out);
  or or_13 (is_jump, comparator_24_eq, comparator_25_eq, comparator_26_eq, or_5_out);
  nor nor_1 (Reg_WE, comparator_24_eq, comparator_5_eq, comparator_6_eq, we_mem, is_bne, is_beq, comparator_26_eq);

  assign rs = Instruction[25:21];
  assign rt = Instruction[20:16];

  // Notes on the sheet:
  //   Funct: 5-0 
  //   shamt: 10-6
  //   rd: 15-11
  //   rt: 20-16
  //   rs: 25-21
  //   Opcode: 31-26
  //   2009000a
  //   Tyeon Ford and Andy Quach
  //   I - Line
  //   checks if opcode is 0
  //   R-type
  //   R - Line
  //   CHECKS OP CODE FOR I - TYPE
  //   CHECKS OP CODE FOR J-TYPE
  //   imm3 or rd
  //   imm2 or shamt
  //   imm1 or funct
  //   rd
  //   sll (R)
  //   andi (I)
  //   or (R)
  //   imm3
  //   add (R)
  //   sub (R)
  //   mult (R)
  //   div (R)
  //   mflo (R)
  //   mfhi (R)
  //   srl (R)
  //   slt (R)
  //   and (R)
  //   ori (I)
  //   xor (R)
  //   xori (I)
  //   nor (R)
  //   lui (I)
  //   lw (I)
  //   sw (I)
  //   bne (I)
  //   beq (I) 
  //   j (j)
  //   jal (j)
  //   jr (R)
  //   jalr (R)
  //   syscall (R)
  //   in binary based on the instruction
  //   if not R-type,
  //   must be I-type or J-type, so gather imm bits
  //   if R-type,
  //   shamt=0
  //   Everything below this is generating the instruction's code
  //   is_jr
  //   is_jalr
  //   if R-type, rt -> rt and rd -> rd
  //   else (I-type), rt -> rd
  //   ALU CODES:
  //   = 0 = 0000
  //   = 1 = 0001
  //   = 2 = 0010
  //   = 3 = 0011
  //   = 4 = 0100
  //   = 5 = 0101 
  //   = 6 = 0110
  //   = 7 = 0111
  //   = 8 = 1000
  //   = 9 = 1001
  //   = 10 = 1010
  //   = 11 = 1011
  //   = 12 = 1100
  //   = 13 = 1101
  //   either I-type or sll or srl
  //   NO REG WE
  //   = 1 if R-type
  //   if jal then rd = $ra
  //   Final ALU code
  //   = 1 if I-type
  //   if addi, ori, or xori, then use imm.
  //   if jalr
  //   if rd = 0, rd = ra
  //   else rd = rd
  //   NO REG WE
  //   Any I-type will have ALU _code of zero.
  //   unless andi, ori, xori, lui
  //   jal or jalr
  //   Generates reg_write_e
  //   writes unless its mult, div, sw, beq, bne
endmodule

module LEDController (
  input  [31:0] DataFromBus,
  input  [25:0] AddressFromBus,
  input  WriteEnableFromBus,
  output DataToLED
);

  wire and_1_out, clock_1_out, comparator_1_eq;
  wire [31:1] register_1_q;

  Comparator #(.mode("unsigned"), .width(26)) comparator_1 (
    .a(AddressFromBus), .b(26'h3ffff10), .eq(comparator_1_eq));  // open: gt, lt
  and and_1 (and_1_out, comparator_1_eq, WriteEnableFromBus);
  Register #(.width(32)) register_1 (
    .D(DataFromBus), .en(and_1_out), .clk(clock_1_out), .Q({register_1_q, DataToLED}));  // open: clr
  Clock clock_1 (.out(clock_1_out));
  // Probe on {register_1_q, DataToLED}
  // Probe on DataToLED

  // Notes on the sheet:
  //   One led or multiple?
endmodule

module JoyStickController (
  input  [31:0] DataFromBus,
  input  WEFromBus,
  input  [25:0] AddressFromBus,
  input  [3:0] X,
  input  [3:0] Y,
  output WriteToBus,
  output [31:0] DataToBus
);

  wire comparator_1_eq, comparator_2_eq, not_1_out, or_1_out;
  wire [3:0] multiplexer_1_out;

  Comparator #(.mode("unsigned"), .width(26)) comparator_1 (
    .a(26'h3ffff50), .b(AddressFromBus), .eq(comparator_1_eq));  // open: gt, lt
  Comparator #(.mode("unsigned"), .width(26)) comparator_2 (
    .a(AddressFromBus), .b(26'h3ffff54), .eq(comparator_2_eq));  // open: gt, lt
  Multiplexer #(.width(4)) multiplexer_1 (.in0(X), .in1(Y), .out(multiplexer_1_out), .sel(comparator_2_eq));
  not not_1 (not_1_out, WEFromBus);
  or or_1 (or_1_out, comparator_1_eq, comparator_2_eq);
  assign DataToBus = {{28{1'b0}}, multiplexer_1_out};  // Bit_Extender bit_extender_1
  and and_1 (WriteToBus, not_1_out, or_1_out);

  // Notes on the sheet:
  //   X Address
  //   Y Address
endmodule

module HexController (
  input  [31:0] DataFromBus,
  input  [25:0] AddressFromBus,
  input  WriteEnable,
  output [3:0] DataToShow
);

  wire and_1_out, comparator_1_eq;

  // Probe on DataFromBus[3:0]
  Comparator #(.mode("unsigned"), .width(26)) comparator_1 (
    .a(AddressFromBus), .b(26'h3ffff30), .eq(comparator_1_eq));  // open: gt, lt
  Register #(.width(4)) register_1 (.D(DataFromBus[3:0]), .clk(and_1_out), .Q(DataToShow));  // open: en, clr
  and and_1 (and_1_out, comparator_1_eq, WriteEnable);
endmodule
