// Logisim project ProjectBusLayout.circ as structural Verilog: 12 circuits, main circuit Computer
module Computer (
);

  wire clock_1_out, clock_2_out, clock_3_out, cpu_1_buswriteenable, keyboard_1_avail,
       keyboardcontroller_1_keyboardread, keyboardcontroller_1_writetobus, ledcontroller_1_datatoled,
       memorycontroller_1_writeenabletomem, memorycontroller_1_writetobus, rgb_video_1_p1, rgb_video_1_p2,
       rgbledcontroller_1_blue, rgbledcontroller_1_green, rgbledcontroller_1_red,
       terminalcontroller_1_writetoterminal;
  wire [3:0] hexcontroller_1_datatoscreen;
  wire [6:0] keyboard_1_data, terminalcontroller_1_datatoterminal;
  wire [7:0] rgb_video_1_p3, rgb_video_1_p4;
  wire [23:0] memorycontroller_1_addresstomem, rgb_video_1_p5;
  wire [25:0] cpu_1_addresstobus;
  wire [31:0] controlled_buffer_1_out, cpu_1_datatobus, keyboardcontroller_1_datatobus,
       memorycontroller_1_datatobus, memorycontroller_1_datatomem, ram_1_dout;

  RAM #(.addrWidth(24), .dataWidth(32), .enables("line")) ram_1 (
    .addr(memorycontroller_1_addresstomem), .we(memorycontroller_1_writeenabletomem), .clk(clock_1_out),
    .din(memorycontroller_1_datatomem), .dout(ram_1_dout));
  Clock clock_1 (.out(clock_1_out));
  Clock clock_2 (.out(clock_2_out));
  Keyboard keyboard_1 (
    .clk(clock_2_out), .re(keyboardcontroller_1_keyboardread), .avail(keyboard_1_avail),
    .data(keyboard_1_data));  // open: clr
  MemoryController memorycontroller_1 (
    .WriteEnableFromBus(cpu_1_buswriteenable), .AddressFromBus(cpu_1_addresstobus),
    .DataFromBus(controlled_buffer_1_out), .DataFromMem(ram_1_dout),
    .DataToBus(memorycontroller_1_datatobus), .AddressToMem(memorycontroller_1_addresstomem),
    .DataToMem(memorycontroller_1_datatomem), .WriteToBus(memorycontroller_1_writetobus),
    .WriteEnableToMem(memorycontroller_1_writeenabletomem));
  CPU cpu_1 (
    .DataFromBus(controlled_buffer_1_out), .DataToBus(cpu_1_datatobus), .AddressToBus(cpu_1_addresstobus),
    .BusWriteEnable(cpu_1_buswriteenable));
  assign controlled_buffer_1_out = memorycontroller_1_writetobus ? memorycontroller_1_datatobus : 32'bz;  // Controlled_Buffer controlled_buffer_1
  assign controlled_buffer_1_out = cpu_1_buswriteenable ? cpu_1_datatobus : 32'bz;  // Controlled_Buffer controlled_buffer_2
  KeyboardController keyboardcontroller_1 (
    .KeyboardData(keyboard_1_data), .KeyboardStatus(keyboard_1_avail), .DataFromBus(controlled_buffer_1_out),
    .WriteEnableFromBus(cpu_1_buswriteenable), .AddressFromBus(cpu_1_addresstobus),
    .WriteToBus(keyboardcontroller_1_writetobus), .DataToBus(keyboardcontroller_1_datatobus),
    .KeyboardRead(keyboardcontroller_1_keyboardread));
  assign controlled_buffer_1_out = keyboardcontroller_1_writetobus ? keyboardcontroller_1_datatobus : 32'bz;  // Controlled_Buffer controlled_buffer_3
  Clock clock_3 (.out(clock_3_out));
  TTY tty_1 (
    .data(terminalcontroller_1_datatoterminal), .clk(clock_3_out), .we(terminalcontroller_1_writetoterminal));  // open: clr
  // RGB_Video #(.height(256), .scale(1), .width(256)) rgb_video_1: pin names not known; wires that end beside it: rgb_video_1_p1, rgb_video_1_p2, rgb_video_1_p3, rgb_video_1_p4, rgb_video_1_p5
  Clock clock_4 (.out(rgb_video_1_p1));
  TerminalController terminalcontroller_1 (
    .WriteEnableFromBus(cpu_1_buswriteenable), .AddressFromBus(cpu_1_addresstobus),
    .DataFromBus(controlled_buffer_1_out), .DataToTerminal(terminalcontroller_1_datatoterminal),
    .WriteToTerminal(terminalcontroller_1_writetoterminal));
  RGBController rgbcontroller_1 (
    .AddressFromBus(cpu_1_addresstobus), .DataFromBus(controlled_buffer_1_out),
    .WriteEnable(cpu_1_buswriteenable), .RGBX(rgb_video_1_p3), .RGBY(rgb_video_1_p4),
    .RGBColor(rgb_video_1_p5), .RGBWrite(rgb_video_1_p2));
  RGBLEDController rgbledcontroller_1 (
    .AddressFromBus(cpu_1_addresstobus), .DataFromBus(controlled_buffer_1_out),
    .WriteEnable(cpu_1_buswriteenable), .Green(rgbledcontroller_1_green), .Red(rgbledcontroller_1_red),
    .Blue(rgbledcontroller_1_blue));
  HEXController hexcontroller_1 (
    .AddressFromBus(cpu_1_addresstobus), .DataFromBus(controlled_buffer_1_out),
    .WriteEnable(cpu_1_buswriteenable), .DataToScreen(hexcontroller_1_datatoscreen));
  LEDController ledcontroller_1 (
    .AddressFromBus(cpu_1_addresstobus), .DataFromBus(controlled_buffer_1_out),
    .WriteEnable(cpu_1_buswriteenable), .DataToLED(ledcontroller_1_datatoled));
  // RGBLED rgbled_1: pin names not known; wires that end beside it: rgbledcontroller_1_red, rgbledcontroller_1_green, rgbledcontroller_1_blue
  Hex_Digit_Display hex_digit_display_1 (.value(hexcontroller_1_datatoscreen));  // open: dp
  LED led_1 (.in(ledcontroller_1_datatoled));

  // Notes on the sheet:
  //   Write_enable
  //   Address
  //   Data
endmodule

module CPU (
  input  [31:0] DataFromBus,
  output [31:0] DataToBus,
  output [25:0] AddressToBus,
  output BusWriteEnable
);

  wire alu_1_is_equal, and_1_out, and_2_out, clock_1_out, clock_2_out, control_1_aluvsmemselect,
       control_1_beq, control_1_bne, control_1_imm_sel, control_1_j, control_1_jal, control_1_jalr,
       control_1_jr, control_1_reg_write_e, not_1_out, or_1_out, or_2_out, or_3_out, or_4_out;
  wire [3:0] control_1_alu_code;
  wire [4:0] control_1_rd, control_1_rs, control_1_rt;
  wire [15:0] bit_extender_3_out, bit_extender_4_out, shifter_1_out;
  wire [23:0] bit_extender_8_out;
  wire [25:0] bit_extender_5_out, control_1_imm, shifter_2_out;
  wire [31:0] adder_1_out, adder_2_out, alu_1_res, bit_extender_1_out, bit_extender_2_out,
       bit_extender_6_out, multiplexer_1_out, multiplexer_2_out, multiplexer_3_out, multiplexer_4_out,
       multiplexer_5_out, multiplexer_6_out, regfile_1_rs_data, register_1_q, rom_1_data, shifter_3_out,
       shifter_4_out;

  Shifter #(.width(16)) shifter_1 (.in(bit_extender_3_out), .\dist (4'b0010), .out(shifter_1_out));
  Adder #(.width(32)) adder_1 (.a(register_1_q), .b(32'h4), .out(adder_1_out));  // open: cin, cout
  assign bit_extender_1_out = {{16{shifter_1_out[15]}}, shifter_1_out};  // Bit_Extender bit_extender_1
  Shifter #(.width(26)) shifter_2 (.in(bit_extender_5_out), .\dist (5'b00010), .out(shifter_2_out));
  Adder #(.width(32)) adder_2 (.a(adder_1_out), .b(bit_extender_1_out), .out(adder_2_out));  // open: cin, cout
  assign bit_extender_2_out = {{6{shifter_2_out[25]}}, shifter_2_out};  // Bit_Extender bit_extender_2
  Multiplexer #(.width(32)) multiplexer_1 (
    .in0(bit_extender_2_out), .in1(regfile_1_rs_data), .out(multiplexer_1_out), .sel(or_1_out));
  Shifter #(.shift("lr"), .width(32)) shifter_3 (.in(register_1_q), .\dist (5'b00010), .out(shifter_3_out));
  Multiplexer #(.width(32)) multiplexer_2 (
    .in0(adder_1_out), .in1(adder_2_out), .out(multiplexer_2_out), .sel(or_2_out));
  Multiplexer #(.width(32)) multiplexer_3 (
    .in0(multiplexer_2_out), .in1(multiplexer_1_out), .out(multiplexer_3_out), .sel(or_3_out));
  Clock clock_1 (.out(clock_1_out));
  Bit_Extender #(.in_width(26)) bit_extender_3 (.in(control_1_imm), .out(bit_extender_3_out));
  Bit_Extender #(.in_width(32)) bit_extender_4 (.in(shifter_3_out), .out(bit_extender_4_out));
  Register #(.width(32)) register_1 (
    .D(multiplexer_3_out), .en(1'b1), .clk(clock_1_out), .Q(register_1_q));  // open: clr
  ROM #(.addrWidth(16), .dataWidth(32)) rom_1 (.addr(bit_extender_4_out), .data(rom_1_data));
  // Probe on rom_1_data
  Bit_Extender #(.in_width(32), .out_width(26)) bit_extender_5 (.in(rom_1_data), .out(bit_extender_5_out));
  Multiplexer #(.width(32)) multiplexer_4 (
    .in0(alu_1_res), .in1(DataFromBus), .out(multiplexer_4_out), .sel(control_1_aluvsmemselect));
  or or_1 (or_1_out, control_1_jr, control_1_jalr);
  Multiplexer #(.width(32)) multiplexer_5 (
    .in0(multiplexer_4_out), .in1(adder_1_out), .out(multiplexer_5_out), .sel(or_4_out));
  or or_2 (or_2_out, and_1_out, and_2_out);
  and and_1 (and_1_out, not_1_out, control_1_bne);
  and and_2 (and_2_out, alu_1_is_equal, control_1_beq);
  regfile regfile_1 (
    .rd(control_1_rd), .rs(control_1_rs), .rt(control_1_rt), .rd_data(multiplexer_5_out),
    .write_e(control_1_reg_write_e), .rs_data(regfile_1_rs_data), .rt_data(DataToBus));
  not not_1 (not_1_out, alu_1_is_equal);
  or or_3 (or_3_out, control_1_jr, control_1_j, control_1_jal, control_1_jalr);
  or or_4 (or_4_out, control_1_jal, control_1_jalr);
  Control control_1 (
    .Inst(rom_1_data), .rs(control_1_rs), .rt(control_1_rt), .rd(control_1_rd), .imm(control_1_imm),
    .imm_sel(control_1_imm_sel), .reg_write_e(control_1_reg_write_e), .ALU_code(control_1_alu_code),
    .jalr(control_1_jalr), .jr(control_1_jr), .ALUvsMEMselect(control_1_aluvsmemselect), .beq(control_1_beq),
    .bne(control_1_bne), .we_mem(BusWriteEnable), .jal(control_1_jal), .j(control_1_j));
  assign bit_extender_6_out = {{6{control_1_imm[25]}}, control_1_imm};  // Bit_Extender bit_extender_6
  Multiplexer #(.width(32)) multiplexer_6 (
    .in0(DataToBus), .in1(bit_extender_6_out), .out(multiplexer_6_out), .sel(control_1_imm_sel));
  ALU alu_1 (
    .OP1(regfile_1_rs_data), .OP2(multiplexer_6_out), .ALU_CODE(control_1_alu_code), .Res(alu_1_res),
    .is_equal(alu_1_is_equal));
  Bit_Extender #(.in_width(32), .out_width(26)) bit_extender_7 (.in(alu_1_res), .out(AddressToBus));
  Shifter #(.shift("lr"), .width(32)) shifter_4 (.in(alu_1_res), .\dist (5'b00010), .out(shifter_4_out));
  Bit_Extender #(.in_width(32), .out_width(24)) bit_extender_8 (.in(shifter_4_out), .out(bit_extender_8_out));
  Clock clock_2 (.out(clock_2_out));
  // RAM #(.addrWidth(24), .dataWidth(32)) ram_1: pin names not known; wires that end beside it: bit_extender_8_out, BusWriteEnable, clock_2_out, DataToBus

  // Notes on the sheet:
  //   offset:(word addressed)
  //   label: for j, jal (word addressed)
  //   PC+4+Offset
  //   register for jr, jalr (byte addressed)
  //   any jump
  //   contents of rom_1 (hex, n*v repeats v):
  //   20080001 ac08ff30 ac08ff34 ac00ff34 ac08ff38 ac00ff38 ac08ff3c ac00ff3c ac08ff10 ac08ff14 8c08ff14
  //   8c08ff10 800000c
  //   ALU
  //   PC+4
  //   MEM
  //   jr/jalr
  //   jal/jalr
  //   jal/jalr
  //   bne
  //   beq
  //   address right?
endmodule

module MemoryController (
  input  WriteEnableFromBus,
  input  [25:0] AddressFromBus,
  input  [31:0] DataFromBus,
  input  [31:0] DataFromMem,
  output [31:0] DataToBus,
  output WriteToBus,
  output WriteEnableToMem,
  output [23:0] AddressToMem,
  output [31:0] DataToMem
);

  wire comparator_1_lt, not_1_out;
  wire [25:0] shifter_1_out;

  Comparator #(.mode("unsigned"), .width(26)) comparator_1 (
    .a(AddressFromBus), .b(26'h3ffff00), .lt(comparator_1_lt));  // open: gt, eq
  not not_1 (not_1_out, WriteEnableFromBus);
  and and_1 (WriteToBus, not_1_out, comparator_1_lt);
  and and_2 (WriteEnableToMem, WriteEnableFromBus, comparator_1_lt);
  Shifter #(.shift("lr"), .width(26)) shifter_1 (.in(AddressFromBus), .\dist (5'b00010), .out(shifter_1_out));
  Bit_Extender #(.in_width(26), .out_width(24)) bit_extender_1 (.in(shifter_1_out), .out(AddressToMem));

  assign DataToBus = DataFromMem;
  assign DataToMem = DataFromBus;
endmodule

module KeyboardController (
  input  [31:0] DataFromBus,
  input  WriteEnableFromBus,
  input  [25:0] AddressFromBus,
  input  [6:0] KeyboardData,
  input  KeyboardStatus,
  output WriteToBus,
  output [31:0] DataToBus,
  output KeyboardRead
);

  wire and_2_out, comparator_1_eq, comparator_2_eq, not_1_out, not_2_out;
  wire [31:0] bit_extender_1_out, bit_extender_2_out, multiplexer_1_out;

  assign bit_extender_1_out = {{25{1'b0}}, KeyboardData};  // Bit_Extender bit_extender_1
  assign bit_extender_2_out = {{31{1'b0}}, KeyboardStatus};  // Bit_Extender bit_extender_2
  Comparator #(.mode("unsigned"), .width(26)) comparator_1 (
    .a(AddressFromBus), .b(26'h3ffff10), .eq(comparator_1_eq));  // open: gt, lt
  Comparator #(.mode("unsigned"), .width(26)) comparator_2 (
    .a(AddressFromBus), .b(26'h3ffff14), .eq(comparator_2_eq));  // open: gt, lt
  not not_1 (not_1_out, WriteEnableFromBus);
  and and_1 (KeyboardRead, WriteEnableFromBus, comparator_1_eq);
  and and_2 (and_2_out, not_1_out, comparator_1_eq);
  or or_1 (WriteToBus, and_2_out, comparator_2_eq);
  not not_2 (not_2_out, WriteEnableFromBus);
  Multiplexer #(.width(32)) multiplexer_1 (
    .in0(bit_extender_2_out), .in1(bit_extender_1_out), .out(multiplexer_1_out), .sel(comparator_2_eq));
  Multiplexer #(.width(32)) multiplexer_2 (
    .in0(DataFromBus), .in1(multiplexer_1_out), .out(DataToBus), .sel(not_2_out));

  // Notes on the sheet:
  //   This part might not be necessary
endmodule

module RGBController (
  input  [25:0] AddressFromBus,
  input  [31:0] DataFromBus,
  input  WriteEnable,
  output [7:0] RGBX,
  output [7:0] RGBY,
  output [23:0] RGBColor,
  output RGBWrite
);

  wire and_1_out, and_2_out, and_3_out, clock_1_out, comparator_1_eq, comparator_2_eq, comparator_3_eq,
       comparator_4_eq;
  wire [7:0] bit_extender_1_out;
  wire [23:0] bit_extender_2_out;

  Comparator #(.mode("unsigned"), .width(26)) comparator_1 (
    .a(AddressFromBus), .b(26'h3ffff20), .eq(comparator_1_eq));  // open: gt, lt
  Comparator #(.mode("unsigned"), .width(26)) comparator_2 (
    .a(AddressFromBus), .b(26'h3ffff24), .eq(comparator_2_eq));  // open: gt, lt
  Comparator #(.mode("unsigned"), .width(26)) comparator_3 (
    .a(AddressFromBus), .b(26'h3ffff28), .eq(comparator_3_eq));  // open: gt, lt
  Comparator #(.mode("unsigned"), .width(26)) comparator_4 (
    .a(AddressFromBus), .b(26'h3ffff2c), .eq(comparator_4_eq));  // open: gt, lt
  Clock clock_1 (.out(clock_1_out));
  and and_1 (and_1_out, comparator_1_eq, WriteEnable);
  and and_2 (and_2_out, comparator_2_eq, WriteEnable);
  and and_3 (and_3_out, comparator_3_eq, WriteEnable);
  and and_4 (RGBWrite, comparator_4_eq, WriteEnable);
  Bit_Extender #(.in_width(32), .out_width(8), .\type ("zero")) bit_extender_1 (
    .in(DataFromBus), .out(bit_extender_1_out));
  Register X (.D(bit_extender_1_out), .en(and_1_out), .clk(clock_1_out), .Q(RGBX));  // open: clr
  Register Y (.D(bit_extender_1_out), .en(and_2_out), .clk(clock_1_out), .Q(RGBY));  // open: clr
  Register #(.width(24)) RGB (.D(bit_extender_2_out), .en(and_3_out), .clk(clock_1_out), .Q(RGBColor));  // open: clr
  Bit_Extender #(.in_width(32), .out_width(24), .\type ("zero")) bit_extender_2 (
    .in(DataFromBus), .out(bit_extender_2_out));
endmodule

module TerminalController (
  input  WriteEnableFromBus,
  input  [25:0] AddressFromBus,
  input  [31:0] DataFromBus,
  output [6:0] DataToTerminal,
  output WriteToTerminal
);

  wire comparator_1_eq;

  Comparator #(.mode("unsigned"), .width(26)) comparator_1 (
    .a(AddressFromBus), .b(26'h3ffff00), .eq(comparator_1_eq));  // open: gt, lt
  and and_1 (WriteToTerminal, WriteEnableFromBus, comparator_1_eq);
  Bit_Extender #(.in_width(32), .out_width(7)) bit_extender_1 (.in(DataFromBus), .out(DataToTerminal));
endmodule

module regfile (
  input  [4:0] rs,
  input  [4:0] rt,
  input  [4:0] rd,
  input  write_e,
  input  [31:0] rd_data,
  output [31:0] rs_data,
  output [31:0] rt_data
);

  wire and_1_out, and_2_out, and_3_out, and_4_out, and_5_out, and_6_out, and_7_out, and_8_out, and_9_out,
       and_10_out, and_11_out, and_12_out, and_13_out, and_14_out, and_15_out, and_16_out, and_17_out,
       and_18_out, and_19_out, and_20_out, and_21_out, and_22_out, and_23_out, and_24_out, and_25_out,
       and_26_out, and_27_out, and_28_out, and_29_out, and_30_out, and_31_out, clock_1_out,
       demultiplexer_1_out1, demultiplexer_1_out2, demultiplexer_1_out3, demultiplexer_1_out4,
       demultiplexer_1_out5, demultiplexer_1_out6, demultiplexer_1_out7, demultiplexer_1_out8,
       demultiplexer_1_out9, demultiplexer_1_out10, demultiplexer_1_out11, demultiplexer_1_out12,
       demultiplexer_1_out13, demultiplexer_1_out14, demultiplexer_1_out15, demultiplexer_1_out16,
       demultiplexer_1_out17, demultiplexer_1_out18, demultiplexer_1_out19, demultiplexer_1_out20,
       demultiplexer_1_out21, demultiplexer_1_out22, demultiplexer_1_out23, demultiplexer_1_out24,
       demultiplexer_1_out25, demultiplexer_1_out26, demultiplexer_1_out27, demultiplexer_1_out28,
       demultiplexer_1_out29, demultiplexer_1_out30, demultiplexer_1_out31;
  wire [31:0] register_1_q, register_2_q, register_3_q, register_4_q, register_5_q, register_6_q,
       register_7_q, register_8_q, register_9_q, register_10_q, register_11_q, register_12_q, register_13_q,
       register_14_q, register_15_q, register_16_q, register_17_q, register_18_q, register_19_q,
       register_20_q, register_21_q, register_22_q, register_23_q, register_24_q, register_25_q,
       register_26_q, register_27_q, register_28_q, register_29_q, register_30_q, register_31_q;

  Demultiplexer #(.select(5)) demultiplexer_1 (
    .out1(demultiplexer_1_out1), .out2(demultiplexer_1_out2), .out3(demultiplexer_1_out3),
    .out4(demultiplexer_1_out4), .out5(demultiplexer_1_out5), .out6(demultiplexer_1_out6),
    .out7(demultiplexer_1_out7), .out8(demultiplexer_1_out8), .out9(demultiplexer_1_out9),
    .out10(demultiplexer_1_out10), .out11(demultiplexer_1_out11), .out12(demultiplexer_1_out12),
    .out13(demultiplexer_1_out13), .out14(demultiplexer_1_out14), .out15(demultiplexer_1_out15),
    .out16(demultiplexer_1_out16), .out17(demultiplexer_1_out17), .out18(demultiplexer_1_out18),
    .out19(demultiplexer_1_out19), .out20(demultiplexer_1_out20), .out21(demultiplexer_1_out21),
    .out22(demultiplexer_1_out22), .out23(demultiplexer_1_out23), .out24(demultiplexer_1_out24),
    .out25(demultiplexer_1_out25), .out26(demultiplexer_1_out26), .out27(demultiplexer_1_out27),
    .out28(demultiplexer_1_out28), .out29(demultiplexer_1_out29), .out30(demultiplexer_1_out30),
    .out31(demultiplexer_1_out31), .in(1'b1), .sel(rd));  // open: out0
  and and_1 (and_1_out, write_e, demultiplexer_1_out1);
  and and_2 (and_2_out, write_e, demultiplexer_1_out2);
  and and_3 (and_3_out, write_e, demultiplexer_1_out3);
  and and_4 (and_4_out, write_e, demultiplexer_1_out4);
  and and_5 (and_5_out, write_e, demultiplexer_1_out5);
  and and_6 (and_6_out, write_e, demultiplexer_1_out6);
  and and_7 (and_7_out, write_e, demultiplexer_1_out7);
  and and_8 (and_8_out, write_e, demultiplexer_1_out8);
  and and_9 (and_9_out, write_e, demultiplexer_1_out9);
  and and_10 (and_10_out, write_e, demultiplexer_1_out10);
  and and_11 (and_11_out, write_e, demultiplexer_1_out11);
  and and_12 (and_12_out, write_e, demultiplexer_1_out12);
  and and_13 (and_13_out, write_e, demultiplexer_1_out13);
  and and_14 (and_14_out, write_e, demultiplexer_1_out14);
  and and_15 (and_15_out, write_e, demultiplexer_1_out15);
  and and_16 (and_16_out, write_e, demultiplexer_1_out16);
  and and_17 (and_17_out, write_e, demultiplexer_1_out17);
  and and_18 (and_18_out, write_e, demultiplexer_1_out18);
  and and_19 (and_19_out, write_e, demultiplexer_1_out19);
  and and_20 (and_20_out, write_e, demultiplexer_1_out20);
  and and_21 (and_21_out, write_e, demultiplexer_1_out21);
  and and_22 (and_22_out, write_e, demultiplexer_1_out22);
  and and_23 (and_23_out, write_e, demultiplexer_1_out23);
  and and_24 (and_24_out, write_e, demultiplexer_1_out24);
  and and_25 (and_25_out, write_e, demultiplexer_1_out25);
  and and_26 (and_26_out, write_e, demultiplexer_1_out26);
  and and_27 (and_27_out, write_e, demultiplexer_1_out27);
  and and_28 (and_28_out, write_e, demultiplexer_1_out28);
  and and_29 (and_29_out, write_e, demultiplexer_1_out29);
  and and_30 (and_30_out, write_e, demultiplexer_1_out30);
  and and_31 (and_31_out, write_e, demultiplexer_1_out31);
  Clock clock_1 (.out(clock_1_out));
  Register #(.width(32)) register_1 (.D(rd_data), .en(and_1_out), .clk(clock_1_out), .Q(register_1_q));  // open: clr
  Register #(.width(32)) register_2 (.D(rd_data), .en(and_2_out), .clk(clock_1_out), .Q(register_2_q));  // open: clr
  Register #(.width(32)) register_3 (.D(rd_data), .en(and_3_out), .clk(clock_1_out), .Q(register_3_q));  // open: clr
  Register #(.width(32)) register_4 (.D(rd_data), .en(and_4_out), .clk(clock_1_out), .Q(register_4_q));  // open: clr
  Register #(.width(32)) register_5 (.D(rd_data), .en(and_5_out), .clk(clock_1_out), .Q(register_5_q));  // open: clr
  Register #(.width(32)) register_6 (.D(rd_data), .en(and_6_out), .clk(clock_1_out), .Q(register_6_q));  // open: clr
  Register #(.width(32)) register_7 (.D(rd_data), .en(and_7_out), .clk(clock_1_out), .Q(register_7_q));  // open: clr
  Register #(.width(32)) register_8 (.D(rd_data), .en(and_8_out), .clk(clock_1_out), .Q(register_8_q));  // open: clr
  Register #(.width(32)) register_9 (.D(rd_data), .en(and_9_out), .clk(clock_1_out), .Q(register_9_q));  // open: clr
  Register #(.width(32)) register_10 (.D(rd_data), .en(and_10_out), .clk(clock_1_out), .Q(register_10_q));  // open: clr
  Register #(.width(32)) register_11 (.D(rd_data), .en(and_11_out), .clk(clock_1_out), .Q(register_11_q));  // open: clr
  Register #(.width(32)) register_12 (.D(rd_data), .en(and_12_out), .clk(clock_1_out), .Q(register_12_q));  // open: clr
  Register #(.width(32)) register_13 (.D(rd_data), .en(and_13_out), .clk(clock_1_out), .Q(register_13_q));  // open: clr
  Register #(.width(32)) register_14 (.D(rd_data), .en(and_14_out), .clk(clock_1_out), .Q(register_14_q));  // open: clr
  Register #(.width(32)) register_15 (.D(rd_data), .en(and_15_out), .clk(clock_1_out), .Q(register_15_q));  // open: clr
  Register #(.width(32)) register_16 (.D(rd_data), .en(and_16_out), .clk(clock_1_out), .Q(register_16_q));  // open: clr
  Register #(.width(32)) register_17 (.D(rd_data), .en(and_17_out), .clk(clock_1_out), .Q(register_17_q));  // open: clr
  Register #(.width(32)) register_18 (.D(rd_data), .en(and_18_out), .clk(clock_1_out), .Q(register_18_q));  // open: clr
  Register #(.width(32)) register_19 (.D(rd_data), .en(and_19_out), .clk(clock_1_out), .Q(register_19_q));  // open: clr
  Register #(.width(32)) register_20 (.D(rd_data), .en(and_20_out), .clk(clock_1_out), .Q(register_20_q));  // open: clr
  Register #(.width(32)) register_21 (.D(rd_data), .en(and_21_out), .clk(clock_1_out), .Q(register_21_q));  // open: clr
  Register #(.width(32)) register_22 (.D(rd_data), .en(and_22_out), .clk(clock_1_out), .Q(register_22_q));  // open: clr
  Register #(.width(32)) register_23 (.D(rd_data), .en(and_23_out), .clk(clock_1_out), .Q(register_23_q));  // open: clr
  Register #(.width(32)) register_24 (.D(rd_data), .en(and_24_out), .clk(clock_1_out), .Q(register_24_q));  // open: clr
  Register #(.width(32)) register_25 (.D(rd_data), .en(and_25_out), .clk(clock_1_out), .Q(register_25_q));  // open: clr
  Register #(.width(32)) register_26 (.D(rd_data), .en(and_26_out), .clk(clock_1_out), .Q(register_26_q));  // open: clr
  Register #(.width(32)) register_27 (.D(rd_data), .en(and_27_out), .clk(clock_1_out), .Q(register_27_q));  // open: clr
  Register #(.width(32)) register_28 (.D(rd_data), .en(and_28_out), .clk(clock_1_out), .Q(register_28_q));  // open: clr
  Register #(.width(32)) register_29 (.D(rd_data), .en(and_29_out), .clk(clock_1_out), .Q(register_29_q));  // open: clr
  Register #(.width(32)) register_30 (.D(rd_data), .en(and_30_out), .clk(clock_1_out), .Q(register_30_q));  // open: clr
  Register #(.width(32)) register_31 (.D(rd_data), .en(and_31_out), .clk(clock_1_out), .Q(register_31_q));  // open: clr
  Multiplexer #(.select(5), .width(32)) multiplexer_1 (
    .in0({32{1'b0}}), .in1(register_1_q), .in2(register_2_q), .in3(register_3_q), .in4(register_4_q),
    .in5(register_5_q), .in6(register_6_q), .in7(register_7_q), .in8(register_8_q), .in9(register_9_q),
    .in10(register_10_q), .in11(register_11_q), .in12(register_12_q), .in13(register_13_q),
    .in14(register_14_q), .in15(register_15_q), .in16(register_16_q), .in17(register_17_q),
    .in18(register_18_q), .in19(register_19_q), .in20(register_20_q), .in21(register_21_q),
    .in22(register_22_q), .in23(register_23_q), .in24(register_24_q), .in25(register_25_q),
    .in26(register_26_q), .in27(register_27_q), .in28(register_28_q), .in29(register_29_q),
    .in30(register_30_q), .in31(register_31_q), .out(rs_data), .sel(rs));
  Multiplexer #(.select(5), .width(32)) multiplexer_2 (
    .in0({32{1'b0}}), .in1(register_1_q), .in2(register_2_q), .in3(register_3_q), .in4(register_4_q),
    .in5(register_5_q), .in6(register_6_q), .in7(register_7_q), .in8(register_8_q), .in9(register_9_q),
    .in10(register_10_q), .in11(register_11_q), .in12(register_12_q), .in13(register_13_q),
    .in14(register_14_q), .in15(register_15_q), .in16(register_16_q), .in17(register_17_q),
    .in18(register_18_q), .in19(register_19_q), .in20(register_20_q), .in21(register_21_q),
    .in22(register_22_q), .in23(register_23_q), .in24(register_24_q), .in25(register_25_q),
    .in26(register_26_q), .in27(register_27_q), .in28(register_28_q), .in29(register_29_q),
    .in30(register_30_q), .in31(register_31_q), .out(rt_data), .sel(rt));
endmodule

module ALU (
  input  [3:0] ALU_CODE,
  input  [31:0] OP1,
  input  [31:0] OP2,
  output is_equal,
  output [31:0] Res
);

  wire clock_1_out, comparator_2_lt, comparator_3_eq, comparator_4_eq, or_2_out;
  wire [4:0] bit_extender_1_out, bit_extender_2_out;
  wire [31:0] adder_1_out, and_1_out, bit_extender_3_out, divider_1_out, divider_1_rem, multiplexer_1_out,
       multiplexer_2_out, multiplier_1_cout, multiplier_1_out, nor_1_out, or_1_out, register_1_q,
       register_2_q, shifter_1_out, shifter_2_out, subtractor_1_out, xor_1_out;

  Bit_Extender #(.in_width(32), .out_width(5), .\type ("zero")) bit_extender_1 (.in(OP2), .out(bit_extender_1_out));
  Bit_Extender #(.in_width(32), .out_width(5), .\type ("zero")) bit_extender_2 (.in(OP2), .out(bit_extender_2_out));
  Comparator #(.width(32)) comparator_1 (.a(OP1), .b(OP2), .eq(is_equal));  // open: gt, lt
  Adder #(.width(32)) adder_1 (.a(OP1), .b(OP2), .out(adder_1_out));  // open: cin, cout
  Subtractor #(.width(32)) subtractor_1 (.a(OP1), .b(OP2), .out(subtractor_1_out));  // open: bin, bout
  Multiplier #(.width(32)) multiplier_1 (
    .a(OP1), .b(OP2), .out(multiplier_1_out), .cout(multiplier_1_cout));  // open: cin
  Divider #(.width(32)) divider_1 (.a(OP1), .b(OP2), .out(divider_1_out), .rem(divider_1_rem));  // open: upper
  Shifter #(.width(32)) shifter_1 (.in(OP1), .\dist (bit_extender_1_out), .out(shifter_1_out));
  Shifter #(.shift("lr"), .width(32)) shifter_2 (.in(OP1), .\dist (bit_extender_2_out), .out(shifter_2_out));
  Comparator #(.width(32)) comparator_2 (.a(OP1), .b(OP2), .lt(comparator_2_lt));  // open: gt, eq
  assign and_1_out = OP1 & OP2;  // AND_Gate and_1, 32 bits wide
  assign or_1_out = OP1 | OP2;  // OR_Gate or_1, 32 bits wide
  assign nor_1_out = ~(OP1 | OP2);  // NOR_Gate nor_1, 32 bits wide
  assign xor_1_out = OP1 ^ OP2;  // XOR_Gate xor_1, 32 bits wide
  assign bit_extender_3_out = {{31{1'b0}}, comparator_2_lt};  // Bit_Extender bit_extender_3
  Comparator #(.width(4)) comparator_3 (.a(ALU_CODE), .b(4'b0010), .eq(comparator_3_eq));  // open: gt, lt
  Comparator #(.width(4)) comparator_4 (.a(ALU_CODE), .b(4'b0011), .eq(comparator_4_eq));  // open: gt, lt
  or or_2 (or_2_out, comparator_3_eq, comparator_4_eq);
  Clock clock_1 (.out(clock_1_out));
  Register #(.width(32)) register_1 (
    .D(multiplexer_1_out), .en(or_2_out), .clk(clock_1_out), .Q(register_1_q));  // open: clr
  Multiplexer #(.width(32)) multiplexer_1 (
    .in0(multiplier_1_out), .in1(divider_1_out), .out(multiplexer_1_out), .sel(comparator_4_eq));
  Register #(.width(32)) register_2 (
    .D(multiplexer_2_out), .en(or_2_out), .clk(clock_1_out), .Q(register_2_q));  // open: clr
  Multiplexer #(.width(32)) multiplexer_2 (
    .in0(multiplier_1_cout), .in1(divider_1_rem), .out(multiplexer_2_out), .sel(comparator_4_eq));
  Multiplexer #(.select(4), .width(32)) multiplexer_3 (
    .in0(adder_1_out), .in1(subtractor_1_out), .in4(register_1_q), .in5(register_2_q), .in6(shifter_1_out),
    .in7(shifter_2_out), .in8(bit_extender_3_out), .in9(and_1_out), .in10(or_1_out), .in11(nor_1_out),
    .in12(xor_1_out), .out(Res), .sel(ALU_CODE));  // open: in2, in3, in13, in14, in15

  // Notes on the sheet:
  //   Overflow
  //   Remainder
  //   sll
  //   srl
  //   slt
endmodule

module Control (
  input  [31:0] Inst,
  output [4:0] rs,
  output [4:0] rt,
  output [4:0] rd,
  output [25:0] imm,
  output imm_sel,
  output reg_write_e,
  output [3:0] ALU_code,
  output jalr,
  output jr,
  output ALUvsMEMselect,
  output beq,
  output bne,
  output we_mem,
  output jal,
  output j
);

  wire and_2_out, and_5_out, and_6_out, and_10_out, and_11_out, and_12_out, comparator_1_eq, comparator_2_eq,
       comparator_3_eq, comparator_4_eq, comparator_5_eq, comparator_6_eq, comparator_7_eq, comparator_8_eq,
       comparator_9_eq, comparator_10_lt, comparator_11_eq, comparator_12_eq, comparator_13_eq,
       comparator_14_eq, comparator_15_eq, comparator_16_eq, comparator_17_eq, comparator_18_eq,
       comparator_19_eq, comparator_20_eq, comparator_21_eq, comparator_22_eq, comparator_23_eq,
       comparator_24_eq, comparator_25_eq, comparator_26_eq, comparator_27_eq, comparator_28_eq,
       comparator_29_eq, comparator_30_eq, comparator_31_eq, comparator_32_eq, multiplexer_3_out, nor_1_out,
       not_1_out, not_2_out, not_3_out, not_4_out, or_2_out, sllORsrl_out;
  wire [3:0] adder_1_out, adder_2_out, adder_3_out, adder_4_out, adder_5_out, adder_6_out, adder_7_out,
       adder_8_out, adder_9_out, adder_10_out, adder_11_out, adder_12_out, adder_13_out, adder_14_out,
       adder_15_out, demultiplexer_5_out0, demultiplexer_5_out1, demultiplexer_6_out0, demultiplexer_6_out1,
       demultiplexer_7_out0, demultiplexer_7_out1, demultiplexer_8_out0, demultiplexer_8_out1,
       demultiplexer_9_out0, demultiplexer_9_out1, demultiplexer_10_out0, demultiplexer_10_out1,
       demultiplexer_11_out0, demultiplexer_11_out1, demultiplexer_12_out0, demultiplexer_12_out1,
       demultiplexer_13_out0, demultiplexer_13_out1, demultiplexer_14_out0, demultiplexer_14_out1,
       demultiplexer_15_out0, demultiplexer_15_out1, demultiplexer_16_out0, demultiplexer_16_out1,
       demultiplexer_17_out0, demultiplexer_17_out1, demultiplexer_18_out0, demultiplexer_18_out1,
       demultiplexer_19_out0, demultiplexer_19_out1, multiplexer_4_out, multiplexer_5_out, multiplexer_6_out,
       multiplexer_7_out, multiplexer_8_out, multiplexer_9_out, multiplexer_10_out, multiplexer_11_out,
       multiplexer_12_out, multiplexer_14_out, multiplexer_15_out, multiplexer_16_out, multiplexer_17_out,
       or_4_out, or_5_out;
  wire [4:0] demultiplexer_1_out0, demultiplexer_2_out0, demultiplexer_2_out1, demultiplexer_3_out0,
       multiplexer_19_out, multiplexer_22_out, multiplexer_23_out;
  wire [5:0] demultiplexer_4_out1, multiplexer_1_out, multiplexer_2_out;
  wire [25:0] bit_extender_1_out, bit_extender_2_out, bit_extender_3_out, bit_extender_4_out,
       multiplexer_20_out, multiplexer_25_out;

  or or_1 (ALUvsMEMselect, bne, beq, and_2_out);
  Comparator #(.width(6)) comparator_1 (.a(6'b000010), .b(Inst[5:0]), .eq(comparator_1_eq));  // open: gt, lt
  Comparator #(.width(6)) comparator_2 (.a(6'b001000), .b(Inst[31:26]), .eq(comparator_2_eq));  // open: gt, lt
  Comparator #(.width(6)) comparator_3 (.a({6{1'b0}}), .b(Inst[31:26]), .eq(comparator_3_eq));  // open: gt, lt
  Multiplexer #(.width(6)) multiplexer_1 (
    .in0(Inst[31:26]), .in1(Inst[5:0]), .out(multiplexer_1_out), .sel(comparator_3_eq));
  Multiplexer #(.width(6)) multiplexer_2 (
    .in0(Inst[5:0]), .in1(Inst[31:26]), .out(multiplexer_2_out), .sel(comparator_3_eq));
  Comparator #(.width(6)) comparator_4 (.a(6'b000010), .b(Inst[31:26]), .eq(comparator_4_eq));  // open: gt, lt
  Comparator #(.width(6)) comparator_5 (.a(6'b000100), .b(Inst[31:26]), .eq(comparator_5_eq));  // open: gt, lt
  Comparator #(.width(6)) comparator_6 (.a(6'b000101), .b(Inst[31:26]), .eq(comparator_6_eq));  // open: gt, lt
  Comparator #(.width(6)) comparator_7 (.a(6'b100011), .b(Inst[31:26]), .eq(comparator_7_eq));  // open: gt, lt
  Comparator #(.width(6)) comparator_8 (.a(6'b101011), .b(Inst[31:26]), .eq(comparator_8_eq));  // open: gt, lt
  and and_1 (jal, not_2_out, comparator_9_eq);
  Comparator #(.width(6)) comparator_9 (.a(6'b000011), .b(Inst[31:26]), .eq(comparator_9_eq));  // open: gt, lt
  or or_2 (or_2_out, jal, j);
  not not_1 (not_1_out, comparator_2_eq);
  not not_2 (not_2_out, comparator_3_eq);
  and and_2 (and_2_out, not_2_out, comparator_7_eq);
  and and_3 (we_mem, not_2_out, comparator_8_eq);
  Comparator #(.mode("unsigned"), .width(5)) comparator_10 (
    .a({5{1'b0}}), .b(Inst[10:6]), .lt(comparator_10_lt));  // open: gt, eq
  Demultiplexer #(.width(5)) demultiplexer_1 (
    .out0(demultiplexer_1_out0), .out1(rt), .in(Inst[20:16]), .sel(not_1_out));
  Demultiplexer #(.width(5)) demultiplexer_2 (
    .out0(demultiplexer_2_out0), .out1(demultiplexer_2_out1), .in(Inst[15:11]), .sel(comparator_3_eq));
  Demultiplexer #(.width(5)) demultiplexer_3 (
    .out0(demultiplexer_3_out0), .in(Inst[10:6]), .sel(comparator_3_eq));  // open: out1
  Demultiplexer #(.width(6)) demultiplexer_4 (
    .out1(demultiplexer_4_out1), .in(multiplexer_1_out), .sel(multiplexer_3_out));  // open: out0
  Multiplexer multiplexer_3 (.in0(not_3_out), .in1(comparator_3_eq), .out(multiplexer_3_out), .sel(comparator_3_eq));
  Comparator #(.width(6)) comparator_11 (.a(6'b001000), .b(Inst[5:0]), .eq(comparator_11_eq));  // open: gt, lt
  and and_4 (jr, comparator_11_eq, comparator_3_eq);
  Comparator #(.width(6)) comparator_12 (.a(6'b001001), .b(Inst[5:0]), .eq(comparator_12_eq));  // open: gt, lt
  and and_5 (and_5_out, comparator_12_eq, comparator_3_eq);
  Comparator #(.width(6)) comparator_13 (.a(6'b001100), .b(Inst[5:0]), .eq(comparator_13_eq));  // open: gt, lt
  and and_6 (and_6_out, comparator_13_eq, comparator_3_eq);
  and and_7 (j, comparator_4_eq, not_2_out);
  and and_8 (beq, comparator_5_eq, not_2_out);
  and and_9 (bne, comparator_6_eq, not_2_out);
  Comparator #(.width(6)) comparator_14 (.a({6{1'b0}}), .b(Inst[5:0]), .eq(comparator_14_eq));  // open: gt, lt
  or or_3 (jalr, and_5_out, and_6_out);
  not not_3 (not_3_out, comparator_3_eq);
  Comparator #(.width(6)) comparator_15 (
    .a(6'b100000), .b(demultiplexer_4_out1), .eq(comparator_15_eq));  // open: gt, lt
  Comparator #(.width(6)) comparator_16 (
    .a(6'b100010), .b(demultiplexer_4_out1), .eq(comparator_16_eq));  // open: gt, lt
  Comparator #(.width(6)) comparator_17 (
    .a(6'b011000), .b(demultiplexer_4_out1), .eq(comparator_17_eq));  // open: gt, lt
  Comparator #(.width(6)) comparator_18 (
    .a(6'b011010), .b(demultiplexer_4_out1), .eq(comparator_18_eq));  // open: gt, lt
  Comparator #(.width(6)) comparator_19 (
    .a(6'b010010), .b(demultiplexer_4_out1), .eq(comparator_19_eq));  // open: gt, lt
  Comparator #(.width(6)) comparator_20 (
    .a(6'b010000), .b(demultiplexer_4_out1), .eq(comparator_20_eq));  // open: gt, lt
  Comparator #(.width(6)) comparator_21 (
    .a({6{1'b0}}), .b(demultiplexer_4_out1), .eq(comparator_21_eq));  // open: gt, lt
  Comparator #(.width(6)) comparator_22 (
    .a(6'b000010), .b(demultiplexer_4_out1), .eq(comparator_22_eq));  // open: gt, lt
  Comparator #(.width(6)) comparator_23 (
    .a(6'b101010), .b(demultiplexer_4_out1), .eq(comparator_23_eq));  // open: gt, lt
  Comparator #(.width(6)) comparator_24 (
    .a(6'b100011), .b(demultiplexer_4_out1), .eq(comparator_24_eq));  // open: gt, lt
  Comparator #(.width(6)) comparator_25 (
    .a(6'b101011), .b(demultiplexer_4_out1), .eq(comparator_25_eq));  // open: gt, lt
  Comparator #(.width(6)) comparator_26 (
    .a(6'b100100), .b(demultiplexer_4_out1), .eq(comparator_26_eq));  // open: gt, lt
  Comparator #(.width(6)) comparator_27 (
    .a(6'b100101), .b(demultiplexer_4_out1), .eq(comparator_27_eq));  // open: gt, lt
  Comparator #(.width(6)) comparator_28 (
    .a(6'b100111), .b(demultiplexer_4_out1), .eq(comparator_28_eq));  // open: gt, lt
  nor nor_1 (nor_1_out, comparator_14_eq, comparator_1_eq, comparator_10_lt);
  and and_10 (and_10_out, comparator_10_lt, comparator_3_eq);
  Demultiplexer #(.width(4)) demultiplexer_5 (
    .out0(demultiplexer_5_out0), .out1(demultiplexer_5_out1), .in(4'b0000), .sel(comparator_15_eq));
  Demultiplexer #(.width(4)) demultiplexer_6 (
    .out0(demultiplexer_6_out0), .out1(demultiplexer_6_out1), .in(adder_1_out), .sel(comparator_16_eq));
  Demultiplexer #(.width(4)) demultiplexer_7 (
    .out0(demultiplexer_7_out0), .out1(demultiplexer_7_out1), .in(adder_2_out), .sel(comparator_17_eq));
  Demultiplexer #(.width(4)) demultiplexer_8 (
    .out0(demultiplexer_8_out0), .out1(demultiplexer_8_out1), .in(adder_3_out), .sel(comparator_18_eq));
  Demultiplexer #(.width(4)) demultiplexer_9 (
    .out0(demultiplexer_9_out0), .out1(demultiplexer_9_out1), .in(adder_4_out), .sel(comparator_19_eq));
  Demultiplexer #(.width(4)) demultiplexer_10 (
    .out0(demultiplexer_10_out0), .out1(demultiplexer_10_out1), .in(adder_5_out), .sel(comparator_20_eq));
  Demultiplexer #(.width(4)) demultiplexer_11 (
    .out0(demultiplexer_11_out0), .out1(demultiplexer_11_out1), .in(adder_6_out), .sel(comparator_21_eq));
  Demultiplexer #(.width(4)) demultiplexer_12 (
    .out0(demultiplexer_12_out0), .out1(demultiplexer_12_out1), .in(adder_7_out), .sel(comparator_22_eq));
  Demultiplexer #(.width(4)) demultiplexer_13 (
    .out0(demultiplexer_13_out0), .out1(demultiplexer_13_out1), .in(adder_8_out), .sel(comparator_23_eq));
  Comparator #(.width(6)) comparator_29 (
    .a(6'b100110), .b(demultiplexer_4_out1), .eq(comparator_29_eq));  // open: gt, lt
  not not_4 (not_4_out, nor_1_out);
  assign bit_extender_1_out = {{21{Inst[10]}}, Inst[10:6]};  // Bit_Extender bit_extender_1
  Demultiplexer #(.width(4)) demultiplexer_14 (
    .out0(demultiplexer_14_out0), .out1(demultiplexer_14_out1), .in(adder_9_out), .sel(comparator_24_eq));
  Demultiplexer #(.width(4)) demultiplexer_15 (
    .out0(demultiplexer_15_out0), .out1(demultiplexer_15_out1), .in(adder_12_out), .sel(comparator_25_eq));
  Demultiplexer #(.width(4)) demultiplexer_16 (
    .out0(demultiplexer_16_out0), .out1(demultiplexer_16_out1), .in(adder_13_out), .sel(comparator_26_eq));
  Demultiplexer #(.width(4)) demultiplexer_17 (
    .out0(demultiplexer_17_out0), .out1(demultiplexer_17_out1), .in(adder_14_out), .sel(comparator_27_eq));
  Demultiplexer #(.width(4)) demultiplexer_18 (
    .out0(demultiplexer_18_out0), .out1(demultiplexer_18_out1), .in(adder_10_out), .sel(comparator_28_eq));
  Demultiplexer #(.width(4)) demultiplexer_19 (
    .out0(demultiplexer_19_out0), .out1(demultiplexer_19_out1), .in(adder_15_out), .sel(comparator_29_eq));
  assign bit_extender_2_out = {{10{demultiplexer_2_out0[4]}}, {demultiplexer_2_out0, demultiplexer_3_out0, multiplexer_2_out}};  // Bit_Extender bit_extender_2
  Adder #(.width(4)) adder_1 (.a(demultiplexer_5_out0), .b(4'b0001), .out(adder_1_out));  // open: cin, cout
  Adder #(.width(4)) adder_2 (.a(demultiplexer_6_out0), .b(4'b0001), .out(adder_2_out));  // open: cin, cout
  Adder #(.width(4)) adder_3 (.a(demultiplexer_7_out0), .b(4'b0001), .out(adder_3_out));  // open: cin, cout
  Adder #(.width(4)) adder_4 (.a(demultiplexer_8_out0), .b(4'b0001), .out(adder_4_out));  // open: cin, cout
  Adder #(.width(4)) adder_5 (.a(demultiplexer_9_out0), .b(4'b0001), .out(adder_5_out));  // open: cin, cout
  Adder #(.width(4)) adder_6 (.a(demultiplexer_10_out0), .b(4'b0001), .out(adder_6_out));  // open: cin, cout
  Adder #(.width(4)) adder_7 (.a(demultiplexer_11_out0), .b(4'b0001), .out(adder_7_out));  // open: cin, cout
  Adder #(.width(4)) adder_8 (.a(demultiplexer_12_out0), .b(4'b0001), .out(adder_8_out));  // open: cin, cout
  Adder #(.width(4)) adder_9 (.a(demultiplexer_13_out0), .b(4'b0001), .out(adder_9_out));  // open: cin, cout
  Adder #(.width(4)) adder_10 (.a(demultiplexer_17_out0), .b(4'b0001), .out(adder_10_out));  // open: cin, cout
  Adder #(.width(4)) adder_11 (.a(demultiplexer_19_out0), .b(4'b0001), .out(adder_11_out));  // open: cin, cout
  // Probe on bit_extender_2_out
  Adder #(.width(4)) adder_12 (.a(demultiplexer_14_out0), .b(4'b0000), .out(adder_12_out));  // open: cin, cout
  Adder #(.width(4)) adder_13 (.a(demultiplexer_15_out0), .b(4'b0000), .out(adder_13_out));  // open: cin, cout
  Adder #(.width(4)) adder_14 (.a(demultiplexer_16_out0), .b(4'b0001), .out(adder_14_out));  // open: cin, cout
  Adder #(.width(4)) adder_15 (.a(demultiplexer_18_out0), .b(4'b0001), .out(adder_15_out));  // open: cin, cout
  and and_11 (and_11_out, comparator_3_eq, comparator_14_eq);
  and and_12 (and_12_out, comparator_1_eq, comparator_3_eq);
  Comparator #(.width(4)) comparator_30 (.a(4'b0011), .b(ALU_code), .eq(comparator_30_eq));  // open: gt, lt
  Comparator #(.width(4)) comparator_31 (.a(4'b0010), .b(ALU_code), .eq(comparator_31_eq));  // open: gt, lt
  Multiplexer #(.width(4)) multiplexer_4 (
    .in0(4'b0000), .in1(demultiplexer_5_out1), .out(multiplexer_4_out), .sel(comparator_15_eq));
  Multiplexer #(.width(4)) multiplexer_5 (
    .in0(4'b0000), .in1(demultiplexer_6_out1), .out(multiplexer_5_out), .sel(comparator_16_eq));
  Multiplexer #(.width(4)) multiplexer_6 (
    .in0(4'b0000), .in1(demultiplexer_7_out1), .out(multiplexer_6_out), .sel(comparator_17_eq));
  Multiplexer #(.width(4)) multiplexer_7 (
    .in0(4'b0000), .in1(demultiplexer_8_out1), .out(multiplexer_7_out), .sel(comparator_18_eq));
  Multiplexer #(.width(4)) multiplexer_8 (
    .in0(4'b0000), .in1(demultiplexer_9_out1), .out(multiplexer_8_out), .sel(comparator_19_eq));
  Multiplexer #(.width(4)) multiplexer_9 (
    .in0(4'b0000), .in1(demultiplexer_10_out1), .out(multiplexer_9_out), .sel(comparator_20_eq));
  Multiplexer #(.width(4)) multiplexer_10 (
    .in0(4'b0000), .in1(demultiplexer_11_out1), .out(multiplexer_10_out), .sel(comparator_21_eq));
  Multiplexer #(.width(4)) multiplexer_11 (
    .in0(4'b0000), .in1(demultiplexer_12_out1), .out(multiplexer_11_out), .sel(comparator_22_eq));
  Multiplexer #(.width(4)) multiplexer_12 (
    .in0(4'b0000), .in1(demultiplexer_13_out1), .out(multiplexer_12_out), .sel(comparator_23_eq));
  Multiplexer #(.width(4)) multiplexer_13 (
    .in0(4'b0000), .in1(demultiplexer_14_out1), .sel(comparator_24_eq));  // open: out
  Multiplexer #(.width(4)) multiplexer_14 (
    .in0(4'b0000), .in1(demultiplexer_16_out1), .out(multiplexer_14_out), .sel(comparator_26_eq));
  Multiplexer #(.width(4)) multiplexer_15 (
    .in0(4'b0000), .in1(demultiplexer_17_out1), .out(multiplexer_15_out), .sel(comparator_27_eq));
  Multiplexer #(.width(4)) multiplexer_16 (
    .in0(4'b0000), .in1(demultiplexer_18_out1), .out(multiplexer_16_out), .sel(comparator_28_eq));
  Multiplexer #(.width(4)) multiplexer_17 (
    .in0(4'b0000), .in1(demultiplexer_19_out1), .out(multiplexer_17_out), .sel(comparator_29_eq));
  or sllORsrl (sllORsrl_out, and_11_out, and_12_out);
  Multiplexer #(.width(5)) multiplexer_18 (.in0(Inst[25:21]), .in1(rt), .out(rs), .sel(sllORsrl_out));
  Multiplexer #(.width(5)) multiplexer_19 (
    .in0(demultiplexer_1_out0), .in1(demultiplexer_2_out1), .out(multiplexer_19_out), .sel(comparator_3_eq));
  Multiplexer #(.width(26)) multiplexer_20 (
    .in0(bit_extender_2_out), .in1(bit_extender_1_out), .out(multiplexer_20_out), .sel(and_10_out));
  Multiplexer #(.width(4)) multiplexer_21 (
    .in0(4'b0000), .in1(demultiplexer_15_out1), .sel(comparator_25_eq));  // open: out
  Comparator #(.width(4)) comparator_32 (.a(4'b1010), .b(ALU_code), .eq(comparator_32_eq));  // open: gt, lt
  assign or_4_out = multiplexer_4_out | multiplexer_5_out | multiplexer_6_out | multiplexer_7_out | multiplexer_8_out | multiplexer_9_out | multiplexer_10_out | multiplexer_11_out | multiplexer_12_out;  // OR_Gate or_4, 4 bits wide
  assign or_5_out = multiplexer_14_out | multiplexer_15_out | multiplexer_16_out | multiplexer_17_out;  // OR_Gate or_5, 4 bits wide
  Multiplexer #(.width(5)) multiplexer_22 (
    .in0(multiplexer_19_out), .in1(rt), .out(multiplexer_22_out), .sel(and_2_out));
  assign ALU_code = or_4_out | or_5_out;  // OR_Gate or_6, 4 bits wide
  Multiplexer #(.width(5)) multiplexer_23 (
    .in0(multiplexer_22_out), .in1({5{1'b1}}), .out(multiplexer_23_out), .sel(jal));
  nor nor_2 (reg_write_e, bne, comparator_32_eq, beq, comparator_30_eq, we_mem, comparator_31_eq, j);
  Multiplexer #(.width(5)) multiplexer_24 (.in0(multiplexer_23_out), .in1(5'b11010), .out(rd), .sel(and_6_out));
  or or_7 (imm_sel, comparator_2_eq, we_mem, and_2_out, sllORsrl_out, jal, and_6_out);
  assign bit_extender_3_out = {{20{Inst[5]}}, Inst[5:0]};  // Bit_Extender bit_extender_3
  Bit_Extender #(.in_width(32), .out_width(26)) bit_extender_4 (
    .in({{6{1'b0}}, rs, rt, Inst[15:0]}), .out(bit_extender_4_out));
  Multiplexer #(.width(26)) multiplexer_25 (
    .in0(multiplexer_20_out), .in1(bit_extender_4_out), .out(multiplexer_25_out), .sel(or_2_out));
  Multiplexer #(.width(26)) multiplexer_26 (.in0(multiplexer_25_out), .in1(bit_extender_3_out), .out(imm), .sel(jr));

  // Notes on the sheet:
  //   jr imm
  //   special case for lw
  //   special case for beq
  //   special case for bne
  //   special case for sw
  //   special case for jal
  //   jal or j
  //   srl
  //   special case for j
  //   R-type
  //   special case for jr
  //   special case for jalr
  //   syscall
  //   If shamt > 0
  //   sll
  //   sll
  //   add
  //   sub
  //   mult
  //   div
  //   mflo
  //   mfhi
  //   sll
  //   srl
  //   slt
  //   lw
  //   sw
  //   and
  //   or
  //   nor
  //   xor
  //   1 if srl or sll
  //   Make sure ALU doesn't affect regWE for grey instructions in TT that are not lw and sw 
endmodule

module RGBLEDController (
  input  [25:0] AddressFromBus,
  input  [31:0] DataFromBus,
  input  WriteEnable,
  output Green,
  output Red,
  output Blue
);

  wire and_1_out, and_2_out, and_3_out, clock_1_out, comparator_1_eq, comparator_2_eq, comparator_3_eq;
  wire [31:0] register_1_q, register_2_q, register_3_q;

  Comparator #(.mode("unsigned"), .width(26)) comparator_1 (
    .a(AddressFromBus), .b(26'h3ffff34), .eq(comparator_1_eq));  // open: gt, lt
  Comparator #(.mode("unsigned"), .width(26)) comparator_2 (
    .a(AddressFromBus), .b(26'h3ffff38), .eq(comparator_2_eq));  // open: gt, lt
  Comparator #(.mode("unsigned"), .width(26)) comparator_3 (
    .a(AddressFromBus), .b(26'h3ffff3c), .eq(comparator_3_eq));  // open: gt, lt
  Clock clock_1 (.out(clock_1_out));
  and and_1 (and_1_out, comparator_1_eq, WriteEnable);
  and and_2 (and_2_out, comparator_2_eq, WriteEnable);
  and and_3 (and_3_out, comparator_3_eq, WriteEnable);
  Register #(.width(32)) register_1 (
    .D(DataFromBus), .en(and_1_out), .clk(clock_1_out), .Q(register_1_q));  // open: clr
  Register #(.width(32)) register_2 (
    .D(DataFromBus), .en(and_2_out), .clk(clock_1_out), .Q(register_2_q));  // open: clr
  Register #(.width(32)) register_3 (
    .D(DataFromBus), .en(and_3_out), .clk(clock_1_out), .Q(register_3_q));  // open: clr
  Bit_Extender #(.in_width(32), .out_width(1)) bit_extender_1 (.in(register_1_q), .out(Green));
  Bit_Extender #(.in_width(32), .out_width(1)) bit_extender_2 (.in(register_2_q), .out(Red));
  Bit_Extender #(.in_width(32), .out_width(1)) bit_extender_3 (.in(register_3_q), .out(Blue));
endmodule

module HEXController (
  input  [25:0] AddressFromBus,
  input  [31:0] DataFromBus,
  input  WriteEnable,
  output [3:0] DataToScreen
);

  wire and_1_out, comparator_1_eq;
  wire [3:0] bit_extender_1_out;

  Comparator #(.mode("unsigned"), .width(26)) comparator_1 (
    .a(AddressFromBus), .b(26'h3ffff30), .eq(comparator_1_eq));  // open: gt, lt
  Bit_Extender #(.in_width(32), .out_width(4), .\type ("zero")) bit_extender_1 (
    .in(DataFromBus), .out(bit_extender_1_out));
  and and_1 (and_1_out, comparator_1_eq, WriteEnable);
  Multiplexer #(.width(4)) multiplexer_1 (.in0(4'b0000), .in1(bit_extender_1_out), .out(DataToScreen), .sel(and_1_out));
endmodule

module LEDController (
  input  [25:0] AddressFromBus,
  input  [31:0] DataFromBus,
  input  WriteEnable,
  output DataToLED
);

  wire and_1_out, bit_extender_1_out, comparator_1_eq;

  Comparator #(.mode("unsigned"), .width(26)) comparator_1 (
    .a(AddressFromBus), .b(26'h3ffff41), .eq(comparator_1_eq));  // open: gt, lt
  Bit_Extender #(.in_width(32), .out_width(1), .\type ("zero")) bit_extender_1 (
    .in(DataFromBus), .out(bit_extender_1_out));
  and and_1 (and_1_out, comparator_1_eq, WriteEnable);
  Multiplexer multiplexer_1 (.in0(1'b0), .in1(bit_extender_1_out), .out(DataToLED), .sel(and_1_out));
endmodule
